// Logisim project mcu16.circ as structural Verilog: 28 circuits, main circuit main
module main (
  input  Bkpt_Enable
);

  wire ALUSrc, Bus32, Bus32_, Bus64, Bus64_, BusErr, CLK, clock_1_bus, clock_1_halt_2, Continue_out,
       control_1_id, display_controller_1_clk_2, display_controller_1_clr, display_controller_1_we, DispWEn,
       EX, Halt, IF, IsSv, RAMWEn, Step_out, VBus32, VBus64, VPUError, WBus, WFL, WIR, WPC, WReg;
  wire [1:0] AddrSrc, PCSrc, RegDataSrc, RegDSrc;
  wire [2:0] ALUOp;
  wire [3:0] FL_q, FLOut, RegDest, RegRd1, RegRd2;
  wire [4:0] vrd, vrs;
  wire [5:0] vop;
  wire [6:0] display_controller_1_ascii;
  wire [15:0] IR_q, ROMOut;
  wire [23:0] ABus, ALUOut, Breakpoint_q, Imm, multiplexer_1_out, newpc_1_out, PCOut, reginput_1_out,
       RegOut1, RegOut2;
  wire [31:0] RAMOutHi, RAMOutLo, RDBus, VRegOutHi, VRegOutLo, WDBus;

  Button Step (.out(Step_out));
  Button Continue (.out(Continue_out));
  Clock clock_1 (
    .Step(Step_out), .Halt(Halt), .Continue(Continue_out), .CLK(CLK), .Breakpoint(Breakpoint_q),
    .Bkpt_Enable(Bkpt_Enable), .PC(PCOut), .BusError(BusErr), .HALT_2(clock_1_halt_2), .BUS(clock_1_bus),
    .IF(IF), .VPUError(VPUError));
  LED u_HALT (.in(clock_1_halt_2));
  LED BUS (.in(clock_1_bus));
  LED VPU (.in(VPUError));
  Register #(.width(24)) Breakpoint (.Q(Breakpoint_q));  // open: D, en, clk, clr
  VPU vpu_2 (
    .in_4(vrd), .in_5(vrs), .in_6(RAMOutHi), .in_7(RAMOutLo), .in_8(RegOut2), .VRegOutHi(VRegOutHi),
    .VRegOutLo(VRegOutLo), .in_3(vop), .VPUError(VPUError), .VBus64(VBus64), .VBus32(VBus32), .in_2(CLK),
    .in_1(EX));
  RegInput reginput_1 (
    .RegOut2(RegOut2), .RDBus(RDBus), .Imm(Imm), .ALUOut(ALUOut), .Out(reginput_1_out), .RegDataSrc(RegDSrc),
    .Bus32(Bus32_));
  NewPC newpc_1 (.PCOut(PCOut), .Imm(Imm), .RegOut1(RegOut1), .Out(newpc_1_out), .in_4(PCSrc));
  TTY #(.rows(12), .cols(40)) tty_1 (
    .data(display_controller_1_ascii), .clk(display_controller_1_clk_2), .we(display_controller_1_we),
    .clr(display_controller_1_clr));
  Display_Controller display_controller_1 (
    .WDBus(WDBus), .DispWEn(DispWEn), .CLK(CLK), .ASCII(display_controller_1_ascii),
    .CLK_2(display_controller_1_clk_2), .WE(display_controller_1_we), .CLR(display_controller_1_clr),
    .ABus(ABus));
  RAM ram_1 (
    .Addr(ABus), .OutLo32(RAMOutLo), .CLK(CLK), .WEn(RAMWEn), .B32(Bus32), .B64(Bus64), .DataHi32(WDBus),
    .DataLo32(VRegOutLo), .OutHi32(RAMOutHi));
  Register_File register_file_1 (
    .In(reginput_1_out), .WriteEnable(WReg), .Write1(RegDest), .Out1(RegOut1), .Out2(RegOut2), .CLK(CLK),
    .Read1(RegRd1), .Read2(RegRd2), .WritePC(WPC), .InPC(newpc_1_out), .OutPC(PCOut));
  LED u_IF (.in(IF));
  LED ID (.in(control_1_id));
  LED u_EX (.in(EX));
  ROM #(.addrWidth(15), .dataWidth(16)) rom_1 (.addr(ABus[15:1]), .data(ROMOut));  // open: sel
  Bus_Arbiter bus_arbiter_1 (
    .WBus(WBus), .Bus32(Bus32_), .Bus64(Bus64_), .AddrSrc(AddrSrc), .RAMOutHi(RAMOutHi), .ROMOut(ROMOut),
    .PCOut(PCOut), .RegOut1(RegOut1), .RegOut2(RegOut2), .WDBus(WDBus), .RDBus(RDBus), .AddrBus(ABus),
    .BusErr(BusErr), .DispWEn(DispWEn), .RAMWen(RAMWEn), .VRegOutHi(VRegOutHi), .VBus64(VBus64),
    .Bus64_2(Bus64), .VBus32(VBus32), .Bus32_2(Bus32), .IsSv(IsSv));
  Control control_1 (
    .Instruction(IR_q), .Flags(FL_q), .WIR(WIR), .Halt(Halt), .WFL(WFL), .WBus(WBus), .AddrSrc(AddrSrc),
    .Imm(Imm), .RegRd1(RegRd1), .RegRd2(RegRd2), .RegDest(RegDest), .WReg(WReg), .RegDataSrc(RegDSrc),
    .PCSrc(PCSrc), .WPC(WPC), .ALUOp(ALUOp), .CLK(CLK), .ALUSrc(ALUSrc), .IF(IF), .ID(control_1_id), .EX(EX),
    .Bus32(Bus32_), .Bus64(Bus64_), .vrd(vrd), .vrs(vrs), .vop(vop), .IsSv(IsSv));
  Multiplexer #(.width(24), .enable("false")) multiplexer_1 (
    .in0(RegOut2), .in1(Imm), .out(multiplexer_1_out), .sel(ALUSrc));
  Register #(.width(16)) IR (.D(RDBus[31:16]), .en(WIR), .Q(IR_q), .clk(CLK));  // open: clr
  ALU alu_1 (.In1(RegOut1), .In2(multiplexer_1_out), .Flags(FLOut), .Out(ALUOut), .ALUOp(ALUOp));
  Register #(.width(4)) FL (.D(FLOut), .en(WFL), .Q(FL_q), .clk(CLK));  // open: clr
  LED PC_Write (.in(WPC));
  // Probe on PCSrc
  LED Bus_Write (.in(WBus));
  LED RAM_Write (.in(RAMWEn));
  LED Display_Write (.in(DispWEn));
  LED Reg_Write (.in(WReg));
  // Probe on RegDataSrc
  // Probe on RegDest
  // Probe on RegRd1
  // Probe on RegRd2
  // Probe on ALUSrc
  // Probe on PCOut
  // Probe on ABus
  // Probe on RDBus
  // Probe on WDBus
  // Probe on RegOut1
  // Probe on RegOut2
  // Probe on Imm
  // Probe on ALUOut

  // Notes on the sheet:
  //   ROM
  //   contents of rom_1 (hex, n*v repeats v):
  //   17fc 1401 4ae 1000 1001 1002 1003 404 405 5c02 5cb7 0 17fe 1403 1404 c80 580f 17fe 140b 1fce ce9 4a9
  //   890 401 3881 4001 4408 c81 401 2bfd 4001 4403 c81 1c29 57f3 8e9 1c4e 580f 1428 17fe 140b c80 580f
  //   17fe 140b 283d 40a1 4c01 1c71 1d81 1d81 c81 580f 17fe 140b 1fce cef 401 3841 5ff1 401 5fef 8ef 1c4e
  //   580f 17fe 140b 1fce cef 401 38c1 5fe5 401 3881 5fe2 401 3841 5fdf 401 5fdd 8ef 1c4e 580f 17fe 140b
  //   1fce cef 1fce ce9 4a9 890 5fe7 1080 5fcb 1c29 890 5fe2 1080 5fc6 1c29 890 5fdd 1080 5fc1 1c29 890
  //   5fd8 8e9 1c4e 8ef 1c4e 580f 17fe 140b 1fce cef 1fce ce9 4a9 890 3880 5fbd 1080 5fad 890 5fb9 1080
  //   5fa9 1c29 890 3880 5fb3 1080 5fa3 890 5faf 8e9 1c4e 8ef 1c4e 580f 17fe 140b 1fce cef 1fce ce9 4a9
  //   890 5fad 1080 5f91 1c29 890 5fa8 8e9 1c4e 8ef 1c4e 580f 17fe 140b 1fce cef 1fce ce9 4a9 890 3880
  //   5f8d 1080 5f7d 890 5f89 8e9 1c4e 8ef 1c4e 580f 1fce ce9 419 2044 4000 4406 891 c81 1c29 1c28 1ff0
  //   57f8 8e9 1c4e 580f 1fce cef 5c03 8ef 1c4e 580f 1fce cef 1600 3480 3268 1601 3481 3229 2010 3810 1406
  //   1403 1601 3481 3229 5fdb 1400 1601 3481 5f35 8088 1404 1401 8540 1c8a 8541 a802 a803 a804 a805 ac22
  //   b023 b424 b825 1404 1441 8942 1c8a 8943 1c8a 8944 1c8a 8945 1400 1601 3481 3059 5f19 1404 1401 5f58
  //   5f2a 1404 1421 5f54 5f26 1400 1601 3481 3081 5f0c 10ac 5f20 1404 1441 5f49 5f1b 10b4 5f1a 1404 1461
  //   5f43 5f15 10a8 5f14 1404 1481 5f3d 5f0f 10bc 5f0e 1404 14a1 5f37 5f09 8ef 1c4e 580f 16096*0 5465
  //   7374 696e 6720 6172 6974 686d 6574 6963 2e0a 0 496e 7075 7473 3a0a 0 4578 7065 6374 3a0a 2b30 3031
  //   3520 3030 3237 2030 3033 3220 3030 3439 a2d 3030 3042 2030 3031 3920 3030 3245 2030 3033 370a 2a30
  //   3035 3020 3030 4530 2030 3036 3020 3032 3430 a2f 3030 3033 2030 3030 3420 3030 3138 2030 3030 370a
  //   5*2d2d 2d0a 0 10 20 30 40 5 7 2 9
endmodule

module Clock (
  input  Step,
  input  Halt,
  input  Continue,
  input  VPUError,
  input  BusError,
  input  [23:0] Breakpoint,
  input  [23:0] PC,
  input  Bkpt_Enable,
  input  IF,
  output CLK,
  output HALT_2,
  output BUS
);

  wire and_1_out, and_2_out, and_3_out, and_4_out, clock_1_out, comparator_1_eq, d_ff_1_q, not_1_out,
       or_1_out, or_2_out, xor_1_out;

  not not_1 (not_1_out, Continue);
  and and_1 (and_1_out, not_1_out, Continue);
  or or_1 (or_1_out, VPUError, BusError);
  Comparator #(.width(24)) comparator_1 (.a(Breakpoint), .b(PC), .eq(comparator_1_eq));  // open: gt, lt
  xor xor_1 (xor_1_out, Step, clock_1_out);
  Clock_part clock_1 (.out(clock_1_out));
  or or_2 (or_2_out, d_ff_1_q, Halt, and_2_out);
  and and_2 (and_2_out, comparator_1_eq, Bkpt_Enable, IF);
  D_Flip_Flop d_ff_1 (.clk(xor_1_out), .D(or_2_out), .Q(d_ff_1_q), .reset(and_1_out));  // open: Qn, preset, en
  D_Flip_Flop d_ff_2 (.clk(xor_1_out), .D(or_1_out), .Q(BUS));  // open: Qn, preset, en, reset
  and and_3 (and_3_out, Step, d_ff_1_q);
  or or_3 (CLK, and_3_out, and_4_out);
  and and_4 (and_4_out, xor_1_out, ~d_ff_1_q, ~BUS);  // AND_Gate
  or or_4 (HALT_2, d_ff_1_q, BUS);
endmodule

module Register_File (
  input  [23:0] In,
  input  [23:0] InPC,
  input  [3:0] Read1,
  input  WriteEnable,
  input  [3:0] Read2,
  input  CLK,
  input  WritePC,
  input  [3:0] Write1,
  output [23:0] Out1,
  output [23:0] Out2,
  output [23:0] OutPC
);

  wire ABEn, AEn, BEn, CDEn, CEn, DEn, EEn, EFEn, FEn, or_1_out, or_2_out, or_3_out, or_4_out, or_5_out,
       or_6_out, or_7_out, or_8_out, PCEn1, RAEn1, SPEn1;
  wire [15:0] bit_extender_1_out, InACE;
  wire [15:8] A_q, C_q, E_q;
  wire [23:0] ABOut, AOut, BOut, CDOut, COut, DOut, EFOut, EOut, FOut, InPC_t, pull_resistor_1_node,
       pull_resistor_2_node, pull_resistor_3_node, pull_resistor_4_node, pull_resistor_5_node,
       pull_resistor_6_node, pull_resistor_7_node, pull_resistor_8_node, RAOut, SPOut;

  Demultiplexer #(.select(4), .disabled(0), .enable("false")) demultiplexer_1 (
    .out0(AEn), .out1(BEn), .out2(CEn), .out3(DEn), .out4(EEn), .out5(FEn), .out8(CDEn), .out9(EFEn),
    .out10(ABEn), .out13(PCEn1), .out14(SPEn1), .out15(RAEn1), .in(WriteEnable), .sel(Write1));  // open: out6, out7, out11, out12
  assign bit_extender_1_out = {{8{In[23]}}, In[23:16]};  // Bit_Extender bit_extender_1
  Multiplexer #(.width(24), .enable("false")) multiplexer_1 (.in0(In), .in1(InPC), .out(InPC_t), .sel(WritePC));
  Multiplexer #(.width(16), .enable("false")) multiplexer_2 (
    .in0(In[15:0]), .in1(bit_extender_1_out), .out(InACE), .sel(or_1_out));
  or or_1 (or_1_out, ABEn, CDEn, EFEn);
  or or_2 (or_2_out, AEn, ABEn);
  or or_3 (or_3_out, BEn, ABEn);
  or or_4 (or_4_out, CEn, CDEn);
  or or_5 (or_5_out, DEn, CDEn);
  or or_6 (or_6_out, EEn, EFEn);
  or or_7 (or_7_out, FEn, EFEn);
  or or_8 (or_8_out, PCEn1, WritePC);
  assign AOut = {{8{A_q[15]}}, {A_q, ABOut[23:16]}};  // Bit_Extender bit_extender_2
  Register #(.width(16)) A (.D(InACE), .en(or_2_out), .Q({A_q, ABOut[23:16]}), .clk(CLK));  // open: clr
  assign BOut = {{8{ABOut[15]}}, ABOut[15:0]};  // Bit_Extender bit_extender_3
  Register #(.width(16)) B (.D(In[15:0]), .en(or_3_out), .Q(ABOut[15:0]), .clk(CLK));  // open: clr
  Register #(.width(16)) C (.D(InACE), .en(or_4_out), .Q({C_q, CDOut[23:16]}), .clk(CLK));  // open: clr
  assign COut = {{8{C_q[15]}}, {C_q, CDOut[23:16]}};  // Bit_Extender bit_extender_4
  assign DOut = {{8{CDOut[15]}}, CDOut[15:0]};  // Bit_Extender bit_extender_5
  Register #(.width(16)) D (.D(In[15:0]), .en(or_5_out), .Q(CDOut[15:0]), .clk(CLK));  // open: clr
  Register #(.width(16)) E (.D(InACE), .en(or_6_out), .Q({E_q, EFOut[23:16]}), .clk(CLK));  // open: clr
  assign EOut = {{8{E_q[15]}}, {E_q, EFOut[23:16]}};  // Bit_Extender bit_extender_6
  Register #(.width(16)) F (.D(In[15:0]), .en(or_7_out), .Q(EFOut[15:0]), .clk(CLK));  // open: clr
  assign FOut = {{8{EFOut[15]}}, EFOut[15:0]};  // Bit_Extender bit_extender_7
  Register #(.width(24)) PC (.D(InPC_t), .en(or_8_out), .Q(OutPC), .clk(CLK));  // open: clr
  Register #(.width(24)) SP (.D(In), .en(SPEn1), .Q(SPOut), .clk(CLK));  // open: clr
  Register #(.width(24)) RA (.D(In), .en(RAEn1), .Q(RAOut), .clk(CLK));  // open: clr
  Pull_Resistor pull_resistor_1 (.node(pull_resistor_1_node));
  Pull_Resistor pull_resistor_2 (.node(pull_resistor_2_node));
  Pull_Resistor pull_resistor_3 (.node(pull_resistor_3_node));
  Pull_Resistor pull_resistor_4 (.node(pull_resistor_4_node));
  Pull_Resistor pull_resistor_5 (.node(pull_resistor_5_node));
  Pull_Resistor pull_resistor_6 (.node(pull_resistor_6_node));
  Pull_Resistor pull_resistor_7 (.node(pull_resistor_7_node));
  Pull_Resistor pull_resistor_8 (.node(pull_resistor_8_node));
  Multiplexer #(.select(4), .width(24), .enable("false")) multiplexer_3 (
    .in0(AOut), .in1(BOut), .in2(COut), .in3(DOut), .in4(EOut), .in5(FOut), .in6(pull_resistor_1_node),
    .in7(pull_resistor_2_node), .in8(CDOut), .in9(EFOut), .in10(ABOut), .in11(pull_resistor_3_node),
    .in12(pull_resistor_4_node), .in13(OutPC), .in14(SPOut), .in15(RAOut), .out(Out1), .sel(Read1));
  Multiplexer #(.select(4), .width(24), .enable("false")) multiplexer_4 (
    .in0(AOut), .in1(BOut), .in2(COut), .in3(DOut), .in4(EOut), .in5(FOut), .in6(pull_resistor_5_node),
    .in7(pull_resistor_6_node), .in8(CDOut), .in9(EFOut), .in10(ABOut), .in11(pull_resistor_7_node),
    .in12(pull_resistor_8_node), .in13(OutPC), .in14(SPOut), .in15(RAOut), .out(Out2), .sel(Read2));

  // Other names for the same wires on the sheet: CL = CLK; In16[15:0] = In[15:0]; In24[23:0] = In; PCEn2 = WritePC;
  //   PCOut[23:0] = OutPC
endmodule

module RAM (
  input  [31:0] DataHi32,
  input  [31:0] DataLo32,
  input  [23:0] Addr,
  input  CLK,
  input  WEn,
  input  B32,
  input  B64,
  output [31:0] OutHi32,
  output [31:0] OutLo32
);

  wire or_1_out, W0, W1, W2, W3, W64, WBig;
  wire [0:0] subtractor_1_out;
  wire [1:0] Col;
  wire [15:0] D0, D1, D2, D3, In0, In1, In2, In3;
  wire [20:0] Row, Row0, Row1, Row2, Row_1;

  Subtractor #(.width(24)) subtractor_1 (
    .a(Addr), .b(24'h10000), .out({Row, Col, subtractor_1_out[0]}));  // open: bin, bout
  Adder #(.width(21)) adder_1 (.a(Row), .b(21'h1), .out(Row_1));  // open: cin, cout
  Multiplexer #(.select(2), .width(21), .enable("false")) multiplexer_1 (
    .in0(Row), .in1(Row_1), .in2(Row_1), .in3(Row_1), .out(Row0), .sel(Col));
  Multiplexer #(.select(2), .enable("false")) multiplexer_2 (
    .in0(WEn), .in1(W64), .in2(W64), .in3(WBig), .out(W0), .sel(Col));
  Multiplexer #(.select(2), .width(16), .enable("false")) multiplexer_3 (
    .in0(DataHi32[31:16]), .in1(DataLo32[15:0]), .in2(DataLo32[31:16]), .in3(DataHi32[15:0]), .out(In0),
    .sel(Col));
  or or_1 (or_1_out, B64, B32);
  RAM_part #(.addrWidth(21), .dataWidth(16), .bus("separate")) ram_1 (
    .addr(Row0), .din(In0), .data(D0), .str(W0), .clk(CLK));  // open: sel, ld, clr
  and and_1 (W64, WEn, B64);
  and and_2 (WBig, WEn, or_1_out);
  RAM_part #(.addrWidth(21), .dataWidth(16), .bus("separate")) ram_2 (
    .addr(Row1), .din(In1), .data(D1), .str(W1), .clk(CLK));  // open: sel, ld, clr
  Multiplexer #(.select(2), .width(21), .enable("false")) multiplexer_4 (
    .in0(Row), .in1(Row), .in2(Row_1), .in3(Row_1), .out(Row1), .sel(Col));
  Multiplexer #(.select(2), .enable("false")) multiplexer_5 (
    .in0(WBig), .in1(WEn), .in2(W64), .in3(W64), .out(W1), .sel(Col));
  Multiplexer #(.select(2), .width(16), .enable("false")) multiplexer_6 (
    .in0(DataHi32[15:0]), .in1(DataHi32[31:16]), .in2(DataLo32[15:0]), .in3(DataLo32[31:16]), .out(In1),
    .sel(Col));
  Multiplexer #(.select(2), .width(21), .enable("false")) multiplexer_7 (
    .in0(Row), .in1(Row), .in2(Row), .in3(Row_1), .out(Row2), .sel(Col));
  Multiplexer #(.select(2), .enable("false")) multiplexer_8 (
    .in0(W64), .in1(WBig), .in2(WEn), .in3(W64), .out(W2), .sel(Col));
  Multiplexer #(.select(2), .width(16), .enable("false")) multiplexer_9 (
    .in0(DataLo32[31:16]), .in1(DataHi32[15:0]), .in2(DataHi32[31:16]), .in3(DataLo32[15:0]), .out(In2),
    .sel(Col));
  Multiplexer #(.select(2), .width(32), .enable("false")) multiplexer_10 (
    .in0({D0, D1}), .in1({D1, D2}), .in2({D2, D3}), .in3({D3, D0}), .out(OutHi32), .sel(Col));
  RAM_part #(.addrWidth(21), .dataWidth(16), .bus("separate")) ram_3 (
    .addr(Row2), .din(In2), .data(D2), .str(W2), .clk(CLK));  // open: sel, ld, clr
  Multiplexer #(.select(2), .width(32), .enable("false")) multiplexer_11 (
    .in0({D2, D3}), .in1({D3, D0}), .in2({D0, D1}), .in3({D1, D2}), .out(OutLo32), .sel(Col));
  RAM_part #(.addrWidth(21), .dataWidth(16), .bus("separate")) ram_4 (
    .addr(Row), .din(In3), .data(D3), .str(W3), .clk(CLK));  // open: sel, ld, clr
  Multiplexer #(.select(2), .enable("false")) multiplexer_12 (
    .in0(W64), .in1(W64), .in2(WBig), .in3(WEn), .out(W3), .sel(Col));
  Multiplexer #(.select(2), .width(16), .enable("false")) multiplexer_13 (
    .in0(DataLo32[15:0]), .in1(DataLo32[31:16]), .in2(DataHi32[15:0]), .in3(DataHi32[31:16]), .out(In3),
    .sel(Col));

  // Other names for the same wires on the sheet: CL = CLK; DHiLo[15:0] = DataHi32[15:0];
  //   DHiHi[15:0] = DataHi32[31:16]; DLoLo[15:0] = DataLo32[15:0]; DLoHi[15:0] = DataLo32[31:16]; WAny = WEn

  // Notes on the sheet:
  //   subtract 0x10000 so
  //   the data isn't offset
  //   by 0x2000 in the RAMs.
endmodule

module ALU (
  input  [23:0] In1,
  input  [23:0] In2,
  input  [2:0] ALUOp,
  output [3:0] Flags,
  output [23:0] Out
);

  wire [4:0] bit_extender_1_out;
  wire [23:0] adder_1_out, and_1_out, or_1_out, shifter_1_out, shifter_2_out, subtractor_1_out;

  Bit_Extender #(.in_width(24), .out_width(5)) bit_extender_1 (.in(In2), .out(bit_extender_1_out));
  Comparator #(.width(24)) comparator_1 (.a(In1), .b(In2), .gt(Flags[3]), .eq(Flags[2]), .lt(Flags[0]));
  Adder #(.width(24)) adder_1 (.a(In1), .b(In2), .out(adder_1_out));  // open: cin, cout
  Subtractor #(.width(24)) subtractor_1 (.a(In1), .b(In2), .out(subtractor_1_out));  // open: bin, bout
  assign and_1_out = In1 & In2;  // AND_Gate and_1, 24 bits wide
  assign or_1_out = In1 | In2;  // OR_Gate or_1, 24 bits wide
  Shifter #(.width(24)) shifter_1 (.in(In1), .\dist (bit_extender_1_out), .out(shifter_1_out));
  Shifter #(.width(24), .shift("ar")) shifter_2 (.in(In1), .\dist (bit_extender_1_out), .out(shifter_2_out));
  not not_1 (Flags[1], Flags[2]);
  Multiplexer #(.select(3), .width(24), .enable("false")) multiplexer_1 (
    .in0(adder_1_out), .in1(subtractor_1_out), .in2(and_1_out), .in3(or_1_out), .in4(shifter_1_out),
    .in5(shifter_2_out), .out(Out), .sel(ALUOp));  // open: in6, in7
endmodule

module Bus_Arbiter (
  input  WBus,
  input  Bus32,
  input  Bus64,
  input  VBus64,
  input  VBus32,
  input  [1:0] AddrSrc,
  input  [31:0] RAMOutHi,
  input  [15:0] ROMOut,
  input  [23:0] PCOut,
  input  [23:0] RegOut1,
  input  [23:0] RegOut2,
  input  [31:0] VRegOutHi,
  input  IsSv,
  output [31:0] WDBus,
  output [31:0] RDBus,
  output [23:0] AddrBus,
  output BusErr,
  output DispWEn,
  output RAMWen,
  output Bus64_2,
  output Bus32_2
);

  wire and_1_out, and_2_out, chip_selector_2_wen, DispSel, or_3_out, RAMSel, ROMSel;
  wire [23:0] pull_resistor_1_node, pull_resistor_2_node;
  wire [31:0] bit_extender_2_out, multiplexer_1_out, RegOut1_t, shifter_1_out, shifter_2_out;

  assign RegOut1_t = {{8{RegOut1[23]}}, RegOut1};  // Bit_Extender bit_extender_1
  Pull_Resistor #(.pull("X")) pull_resistor_1 (.node(pull_resistor_1_node));
  Pull_Resistor #(.pull("X")) pull_resistor_2 (.node(pull_resistor_2_node));
  Chip_Selector chip_selector_1 (.ID({8{1'b1}}), .Addr(AddrBus), .CSel(DispSel), .WBus(WBus), .WEn(DispWEn));
  Chip_Selector chip_selector_2 (.ID({8{1'b0}}), .Addr(AddrBus), .CSel(ROMSel), .WBus(WBus), .WEn(chip_selector_2_wen));
  RAM_Selector ram_selector_1 (.ROMSel(ROMSel), .DispSel(DispSel), .WBus(WBus), .RAMSel(RAMSel), .RAMWEn16(RAMWen));
  Shifter #(.width(32)) shifter_1 (.in(RegOut1_t), .\dist (5'b10000), .out(shifter_1_out));
  Multiplexer #(.width(32), .enable("false")) multiplexer_1 (
    .in0(shifter_1_out), .in1(RegOut1_t), .out(multiplexer_1_out), .sel(Bus32_2));
  or or_1 (Bus64_2, Bus64, VBus64);
  or or_2 (Bus32_2, Bus32, VBus32);
  assign RDBus = RAMSel ? RAMOutHi : 32'bz;  // Controlled_Buffer controlled_buffer_1
  assign bit_extender_2_out = {{16{1'b0}}, ROMOut};  // Bit_Extender bit_extender_2
  Shifter #(.width(32)) shifter_2 (.in(bit_extender_2_out), .\dist (5'b10000), .out(shifter_2_out));
  assign RDBus = DispSel ? {32{1'b0}} : 32'bz;  // Controlled_Buffer controlled_buffer_2
  Multiplexer #(.select(2), .width(24), .enable("false")) multiplexer_2 (
    .in0(PCOut), .in1(pull_resistor_1_node), .in2(RegOut2), .in3(pull_resistor_2_node), .out(AddrBus),
    .sel(AddrSrc));
  and and_1 (and_1_out, DispSel, ~DispWEn);  // AND_Gate
  and and_2 (and_2_out, chip_selector_2_wen, or_3_out);
  or or_3 (or_3_out, Bus64_2, Bus32_2);
  Multiplexer #(.width(32), .enable("false")) multiplexer_3 (
    .in0(multiplexer_1_out), .in1(VRegOutHi), .out(WDBus), .sel(IsSv));
  assign RDBus = ROMSel ? shifter_2_out : 32'bz;  // Controlled_Buffer controlled_buffer_3
  or or_4 (BusErr, and_1_out, and_2_out);

  // Other names for the same wires on the sheet: ABus[23:0] = AddrBus; Bus32_ = Bus32; Bus32_t = Bus32_2;
  //   Bus64_ = Bus64; Bus64_t = Bus64_2
endmodule

// Reg Input
module RegInput (
  input  [1:0] RegDataSrc,
  input  Bus32,
  input  [23:0] RegOut2,
  input  [31:0] RDBus,
  input  [23:0] Imm,
  input  [23:0] ALUOut,
  output [23:0] Out
);

  wire [23:0] bit_extender_1_out;
  wire [31:0] multiplexer_1_out, shifter_1_out;

  Shifter #(.width(32), .shift("lr")) shifter_1 (.in(RDBus), .\dist (5'b10000), .out(shifter_1_out));
  Multiplexer #(.width(32), .enable("false")) multiplexer_1 (
    .in0(shifter_1_out), .in1(RDBus), .out(multiplexer_1_out), .sel(Bus32));
  Bit_Extender #(.in_width(32), .out_width(24), .\type ("sign")) bit_extender_1 (
    .in(multiplexer_1_out), .out(bit_extender_1_out));
  Multiplexer #(.select(2), .width(24), .enable("false")) multiplexer_2 (
    .in0(RegOut2), .in1(bit_extender_1_out), .in2(Imm), .in3(ALUOut), .out(Out), .sel(RegDataSrc));
endmodule

module NewPC (
  input  [23:0] PCOut,
  input  [23:0] Imm,
  input  [23:0] RegOut1,
  input  [1:0] in_4,
  output [23:0] Out
);

  wire [23:0] PC_2, PC_2_Imm, shifter_1_out;

  Shifter #(.width(24)) shifter_1 (.in(Imm), .\dist (5'b00001), .out(shifter_1_out));
  Adder #(.width(24)) adder_1 (.a(PCOut), .b(24'h2), .out(PC_2));  // open: cin, cout
  Adder #(.width(24)) adder_2 (.a(PCOut), .b(shifter_1_out), .out(PC_2_Imm));  // open: cin, cout
  Multiplexer #(.select(2), .width(24), .enable("false")) multiplexer_1 (
    .in0(PC_2), .in1(PC_2_Imm), .in2(RegOut1), .out(Out), .sel(in_4));  // open: in3

  // Other names for the same wires on the sheet: PCSrc[1:0] = in_4

  // Notes on the sheet:
  //   using pcout+imm<<1 because by the time this value is
  //   calculated, PC has already been incremented
endmodule

module Display_Controller (
  input  [23:0] ABus,
  input  [31:0] WDBus,
  input  DispWEn,
  input  CLK,
  output [6:0] ASCII,
  output CLK_2,
  output WE,
  output CLR
);

  wire comparator_1_eq, comparator_2_eq, comparator_3_eq;

  Comparator #(.width(24)) comparator_1 (.a(24'hff0002), .b(ABus), .eq(comparator_1_eq));  // open: gt, lt
  Comparator #(.width(24)) comparator_2 (.a(24'hff0000), .b(ABus), .eq(comparator_2_eq));  // open: gt, lt
  Comparator #(.width(7)) comparator_3 (.a(WDBus[22:16]), .b(7'b0000001), .eq(comparator_3_eq));  // open: gt, lt
  and and_1 (WE, comparator_1_eq, DispWEn);
  and and_2 (CLR, comparator_2_eq, DispWEn, comparator_3_eq);

  assign ASCII = WDBus[22:16];
  assign CLK_2 = CLK;

  // Other names for the same wires on the sheet: Addr[23:0] = ABus; Data[6:0] = WDBus[22:16]
endmodule

// Instruction Splitter
module Ins_Splitter (
  input  [15:0] In,
  output [5:0] op,
  output [9:0] imm10,
  output [7:0] imm8,
  output [1:0] rda,
  output [5:0] imm6,
  output [3:0] rd,
  output [3:0] rs,
  output [4:0] vrd,
  output [4:0] vrs
);


  assign imm6 = In[9:4];
  assign imm8 = In[9:2];
  assign imm10 = In[9:0];
  assign op = In[15:10];
  assign rd = In[3:0];
  assign rda = In[1:0];
  assign rs = In[7:4];
  assign vrd = In[4:0];
  assign vrs = In[9:5];
endmodule

// RAMSel
module RAM_Selector (
  input  ROMSel,
  input  DispSel,
  input  WBus,
  output RAMSel,
  output RAMWEn16
);

  nor nor_1 (RAMSel, ROMSel, DispSel);
  and and_1 (RAMWEn16, RAMSel, WBus);
endmodule

// CSel
module Chip_Selector (
  input  [7:0] ID,
  input  [23:0] Addr,
  input  WBus,
  output CSel,
  output WEn
);

  Comparator comparator_1 (.a(ID), .b(Addr[23:16]), .eq(CSel));  // open: gt, lt
  and and_1 (WEn, CSel, WBus);
endmodule

module Control (
  input  CLK,
  input  [15:0] Instruction,
  input  [3:0] Flags,
  output WIR,
  output IF,
  output ID,
  output EX,
  output Halt,
  output WFL,
  output WBus,
  output [1:0] AddrSrc,
  output [23:0] Imm,
  output [3:0] RegRd1,
  output [3:0] RegRd2,
  output [3:0] RegDest,
  output WReg,
  output [1:0] RegDataSrc,
  output [1:0] PCSrc,
  output WPC,
  output [2:0] ALUOp,
  output ALUSrc,
  output Bus32,
  output Bus64,
  output [4:0] vrd,
  output [4:0] vrs,
  output [5:0] vop,
  output IsSv
);

  wire and_4_out, and_5_out, comparator_1_eq, comparator_2_eq, isatype_1_q, iscall_1_q, iscall_2_q,
       iscmp_1_q, ishalt_1_q, isjr_1_q, isldst_1_q, isldst_2_q, isregwrite_1_q, isstore_1_q, ShouldJump;
  wire [1:0] multiplexer_4_out, rda, Sequence_q;
  wire [3:0] bit_extender_1_out, multiplexer_3_out, rdOrig, rs;
  wire [5:0] imm6, Op;
  wire [7:0] imm8;
  wire [9:0] imm10;

  Counter #(.width(2), .max('h2)) Sequence (.Q(Sequence_q), .clk(CLK));  // open: load, D, count, carry, clr
  and and_1 (IF, ~Sequence_q[1], ~Sequence_q[0]);  // AND_Gate
  and and_2 (ID, ~Sequence_q[1], Sequence_q[0]);  // AND_Gate
  and and_3 (EX, Sequence_q[1], ~Sequence_q[0]);  // AND_Gate
  Ins_Splitter ins_splitter_1 (
    .In(Instruction), .op(vop), .imm10(imm10), .imm8(imm8), .rda(rda), .imm6(imm6), .rd(rdOrig), .rs(rs),
    .vrd(vrd), .vrs(vrs));
  ShouldJump shouldjump_1 (.Flags(Flags), .Opcode(Op), .Q(ShouldJump));
  Multiplexer #(.width(6), .enable("false")) multiplexer_1 (.in0(vop), .in1({6{1'b1}}), .out(Op), .sel(vop[5]));
  assign bit_extender_1_out = {{2{1'b0}}, rda};  // Bit_Extender bit_extender_1
  Multiplexer #(.width(4), .enable("false")) multiplexer_2 (
    .in0(rdOrig), .in1(bit_extender_1_out), .out(RegRd1), .sel(isatype_1_q));
  IsAType isatype_1 (.Opcode(Op), .Q(isatype_1_q));
  IsHalt ishalt_1 (.Opcode(Op), .Q(ishalt_1_q));
  IsCmp iscmp_1 (.Opcode(Op), .Q(iscmp_1_q));
  IsStore isstore_1 (.Opcode(vop), .Q(isstore_1_q));
  IsLdSt isldst_1 (.Opcode(vop), .Q(isldst_1_q));
  and and_4 (and_4_out, isldst_1_q, EX);
  Multiplexer #(.width(4), .enable("false")) multiplexer_3 (
    .in0(rs), .in1(4'b1101), .out(multiplexer_3_out), .sel(iscall_1_q));
  IsCall iscall_1 (.Opcode(Op), .Q(iscall_1_q));
  Multiplexer #(.width(2), .enable("false")) multiplexer_4 (
    .in0(2'b01), .in1(2'b10), .out(multiplexer_4_out), .sel(isjr_1_q));
  IsJR isjr_1 (.Opcode(Op), .Q(isjr_1_q));
  and and_5 (and_5_out, ShouldJump, EX);
  IsLdSt isldst_2 (.Opcode(Op), .Q(isldst_2_q));
  Comparator #(.width(6), .mode("unsigned")) comparator_1 (
    .a(vop), .b(6'b100001), .eq(comparator_1_eq));  // open: gt, lt
  Comparator #(.width(6), .mode("unsigned")) comparator_2 (
    .a(vop), .b(6'b100010), .eq(comparator_2_eq));  // open: gt, lt
  and and_6 (Halt, ishalt_1_q, EX);
  and and_7 (WFL, iscmp_1_q, EX);
  and and_8 (WBus, isstore_1_q, EX);
  Multiplexer #(.width(2), .enable("false")) multiplexer_5 (.in0(2'b00), .in1(2'b10), .out(AddrSrc), .sel(and_4_out));
  Immediate immediate_1 (.opcode(Op), .imm6(imm6), .imm8(imm8), .imm10(imm10), .Out(Imm));
  Multiplexer #(.width(4), .enable("false")) multiplexer_6 (
    .in0(multiplexer_3_out), .in1(vrs[3:0]), .out(RegRd2), .sel(vop[5]));
  Multiplexer #(.width(4), .enable("false")) multiplexer_7 (
    .in0(RegRd1), .in1(4'b1111), .out(RegDest), .sel(iscall_2_q));
  IsCall iscall_2 (.Opcode(Op), .Q(iscall_2_q));
  IsRegWrite isregwrite_1 (.Opcode(Op), .Q(isregwrite_1_q));
  and and_9 (WReg, isregwrite_1_q, EX);
  RegDataSrc regdatasrc_1 (.Opcode(Op), .Q(RegDataSrc));
  Multiplexer #(.width(2), .enable("false")) multiplexer_8 (
    .in0(multiplexer_4_out), .in1(2'b00), .out(PCSrc), .sel(ID));
  or or_1 (WPC, and_5_out, ID);
  ALUOp aluop_1 (.Opcode(Op), .Q(ALUOp));
  ALUSrc alusrc_1 (.Opcode(Op), .Q(ALUSrc));
  and and_10 (Bus32, isldst_2_q, EX, RegRd1[3]);
  and and_11 (Bus64, comparator_1_eq, EX);
  and and_12 (IsSv, comparator_2_eq, EX);

  assign WIR = IF;

  // Other names for the same wires on the sheet: rd[3:0] = RegRd1; Op4_0[4:0] = vop[4:0]; RealOp[5:0] = vop;
  //   IsVec = vop[5]

  // Notes on the sheet:
  //   op, not realop - don't wanna turn on for lv/sv
  //   force 64-bit read for all lv instructions to have consistent mem output
endmodule

// call?
module IsCall (
  input  [5:0] Opcode,
  output Q
);

  wire comparator_1_eq, comparator_2_eq;

  Comparator #(.width(6)) comparator_1 (.a(Opcode), .b(6'b010111), .eq(comparator_1_eq));  // open: gt, lt
  Comparator #(.width(6)) comparator_2 (.a(Opcode), .b(6'b011000), .eq(comparator_2_eq));  // open: gt, lt
  or or_1 (Q, comparator_1_eq, comparator_2_eq);
endmodule

// st?
module IsStore (
  input  [5:0] Opcode,
  output Q
);

  wire comparator_1_eq, comparator_2_eq;

  Comparator #(.width(6)) comparator_1 (.a(Opcode), .b(6'b000011), .eq(comparator_1_eq));  // open: gt, lt
  Comparator #(.width(6)) comparator_2 (.a(Opcode), .b(6'b100010), .eq(comparator_2_eq));  // open: gt, lt
  or or_1 (Q, comparator_1_eq, comparator_2_eq);
endmodule

// halt?
module IsHalt (
  input  [5:0] Opcode,
  output Q
);

  Comparator #(.width(6)) comparator_1 (.a(Opcode), .b({6{1'b0}}), .eq(Q));  // open: gt, lt
endmodule

// cmp?
module IsCmp (
  input  [5:0] Opcode,
  output Q
);

  wire comparator_1_eq, comparator_2_eq;

  Comparator #(.width(6)) comparator_1 (.a(Opcode), .b(6'b001111), .eq(comparator_1_eq));  // open: gt, lt
  Comparator #(.width(6)) comparator_2 (.a(Opcode), .b(6'b010000), .eq(comparator_2_eq));  // open: gt, lt
  or or_1 (Q, comparator_1_eq, comparator_2_eq);
endmodule

// ld/st?
module IsLdSt (
  input  [5:0] Opcode,
  output Q
);

  wire comparator_1_eq, comparator_2_eq, comparator_3_eq, comparator_4_eq;

  Comparator #(.width(6)) comparator_1 (.a(Opcode), .b(6'b000010), .eq(comparator_1_eq));  // open: gt, lt
  Comparator #(.width(6)) comparator_2 (.a(Opcode), .b(6'b000011), .eq(comparator_2_eq));  // open: gt, lt
  Comparator #(.width(6)) comparator_3 (.a(Opcode), .b(6'b100001), .eq(comparator_3_eq));  // open: gt, lt
  Comparator #(.width(6)) comparator_4 (.a(Opcode), .b(6'b100010), .eq(comparator_4_eq));  // open: gt, lt
  or or_1 (Q, comparator_1_eq, comparator_2_eq, comparator_3_eq, comparator_4_eq);
endmodule

// A-type?
module IsAType (
  input  [5:0] Opcode,
  output Q
);

  wire comparator_1_eq, comparator_2_eq, comparator_3_eq, comparator_4_eq;

  Comparator #(.width(6)) comparator_1 (.a(Opcode), .b(6'b000100), .eq(comparator_1_eq));  // open: gt, lt
  Comparator #(.width(6)) comparator_2 (.a(Opcode), .b(6'b000101), .eq(comparator_2_eq));  // open: gt, lt
  Comparator #(.width(6)) comparator_3 (.a(Opcode), .b(6'b001010), .eq(comparator_3_eq));  // open: gt, lt
  Comparator #(.width(6)) comparator_4 (.a(Opcode), .b(6'b001100), .eq(comparator_4_eq));  // open: gt, lt
  or or_1 (Q, comparator_1_eq, comparator_2_eq, comparator_3_eq, comparator_4_eq);
endmodule

// J-type?
module IsJType (
  input  [5:0] Opcode,
  output Q
);

  wire and_1_out, comparator_1_gt, comparator_2_lt, comparator_3_eq;

  Comparator #(.width(6), .mode("unsigned")) comparator_1 (
    .a(Opcode), .b(6'b010000), .gt(comparator_1_gt));  // open: eq, lt
  Comparator #(.width(6), .mode("unsigned")) comparator_2 (
    .a(Opcode), .b(6'b010110), .lt(comparator_2_lt));  // open: gt, eq
  Comparator #(.width(6), .mode("unsigned")) comparator_3 (
    .a(Opcode), .b(6'b010111), .eq(comparator_3_eq));  // open: gt, lt
  and and_1 (and_1_out, comparator_1_gt, comparator_2_lt);
  or or_1 (Q, and_1_out, comparator_3_eq);
endmodule

// zext?
module IsUnsigned (
  input  [5:0] Opcode,
  output Q
);

  wire comparator_1_eq, comparator_2_eq, comparator_3_eq, comparator_4_eq;

  Comparator #(.width(6)) comparator_1 (.a(Opcode), .b(6'b000101), .eq(comparator_1_eq));  // open: gt, lt
  Comparator #(.width(6)) comparator_2 (.a(Opcode), .b(6'b001101), .eq(comparator_2_eq));  // open: gt, lt
  Comparator #(.width(6)) comparator_3 (.a(Opcode), .b(6'b001110), .eq(comparator_3_eq));  // open: gt, lt
  Comparator #(.width(6)) comparator_4 (.a(Opcode), .b(6'b001100), .eq(comparator_4_eq));  // open: gt, lt
  or or_1 (Q, comparator_1_eq, comparator_2_eq, comparator_3_eq, comparator_4_eq);
endmodule

// jmpr?
module IsJR (
  input  [5:0] Opcode,
  output Q
);

  wire comparator_1_eq, comparator_2_eq;

  Comparator #(.width(6)) comparator_1 (.a(Opcode), .b(6'b010110), .eq(comparator_1_eq));  // open: gt, lt
  Comparator #(.width(6)) comparator_2 (.a(Opcode), .b(6'b011000), .eq(comparator_2_eq));  // open: gt, lt
  or or_1 (Q, comparator_1_eq, comparator_2_eq);
endmodule

// wreg?
module IsRegWrite (
  input  [5:0] Opcode,
  output Q
);

  wire and_1_out, comparator_1_eq, comparator_2_eq, comparator_3_lt, iscall_1_q, nor_1_out;

  Comparator #(.width(6), .mode("unsigned")) comparator_1 (
    .a(Opcode), .b({6{1'b0}}), .eq(comparator_1_eq));  // open: gt, lt
  Comparator #(.width(6), .mode("unsigned")) comparator_2 (
    .a(Opcode), .b(6'b000011), .eq(comparator_2_eq));  // open: gt, lt
  Comparator #(.width(6), .mode("unsigned")) comparator_3 (
    .a(Opcode), .b(6'b001111), .lt(comparator_3_lt));  // open: gt, eq
  nor nor_1 (nor_1_out, comparator_1_eq, comparator_2_eq);
  IsCall iscall_1 (.Opcode(Opcode), .Q(iscall_1_q));
  and and_1 (and_1_out, nor_1_out, comparator_3_lt);
  or or_1 (Q, and_1_out, iscall_1_q);
endmodule

// aluop
module ALUOp (
  input  [5:0] Opcode,
  output [2:0] Q
);

  wire and_1_out, and_2_out, and_3_out, and_4_out, and_5_out, and_6_out, and_7_out, and_8_out, not_1_out,
       not_2_out, not_3_out, not_4_out, not_5_out, not_6_out, not_7_out, not_8_out, not_9_out;

  not not_1 (not_1_out, Opcode[1]);
  not not_2 (not_2_out, Opcode[0]);
  not not_3 (not_3_out, Opcode[2]);
  not not_4 (not_4_out, Opcode[2]);
  not not_5 (not_5_out, Opcode[1]);
  not not_6 (not_6_out, Opcode[0]);
  not not_7 (not_7_out, Opcode[1]);
  not not_8 (not_8_out, Opcode[0]);
  not not_9 (not_9_out, Opcode[2]);
  and and_1 (and_1_out, Opcode[2], not_1_out, Opcode[0]);
  and and_2 (and_2_out, Opcode[3], Opcode[2], Opcode[1], not_2_out);
  and and_3 (and_3_out, not_3_out, Opcode[0]);
  and and_4 (and_4_out, not_4_out, Opcode[1]);
  and and_5 (and_5_out, Opcode[2], not_5_out, not_6_out);
  and and_6 (and_6_out, not_7_out, not_8_out);
  and and_7 (and_7_out, not_9_out, Opcode[1], Opcode[0]);
  and and_8 (and_8_out, Opcode[3], Opcode[2], Opcode[1]);
  or or_1 (Q[2], and_1_out, and_2_out);
  or or_2 (Q[1], and_3_out, and_4_out, and_5_out);
  or or_3 (Q[0], and_6_out, and_7_out, and_8_out);
endmodule

// RDS
module RegDataSrc (
  input  [5:0] Opcode,
  output [1:0] Q
);

  wire and_1_out, and_2_out, and_3_out, and_4_out, not_1_out, not_2_out, not_3_out, not_4_out;

  not not_1 (not_1_out, Opcode[4]);
  not not_2 (not_2_out, Opcode[4]);
  not not_3 (not_3_out, Opcode[4]);
  not not_4 (not_4_out, Opcode[4]);
  and and_1 (and_1_out, not_1_out, Opcode[2]);
  and and_2 (and_2_out, not_2_out, Opcode[3]);
  and and_3 (and_3_out, not_3_out, Opcode[1]);
  and and_4 (and_4_out, not_4_out, Opcode[3]);
  or or_1 (Q[1], and_1_out, and_2_out);
  or or_2 (Q[0], and_3_out, and_4_out);
endmodule

module Immediate (
  input  [5:0] opcode,
  input  [5:0] imm6,
  input  [7:0] imm8,
  input  [9:0] imm10,
  output [23:0] Out
);

  wire isatype_1_q, isjtype_1_q, isunsigned_1_q, isunsigned_2_q;
  wire [23:0] bit_extender_1_out, bit_extender_2_out, bit_extender_3_out, bit_extender_4_out,
       bit_extender_5_out, multiplexer_1_out, multiplexer_2_out, multiplexer_3_out;

  assign bit_extender_1_out = {{18{imm6[5]}}, imm6};  // Bit_Extender bit_extender_1
  assign bit_extender_2_out = {{18{1'b0}}, imm6};  // Bit_Extender bit_extender_2
  assign bit_extender_3_out = {{16{imm8[7]}}, imm8};  // Bit_Extender bit_extender_3
  assign bit_extender_4_out = {{16{1'b0}}, imm8};  // Bit_Extender bit_extender_4
  assign bit_extender_5_out = {{14{imm10[9]}}, imm10};  // Bit_Extender bit_extender_5
  Multiplexer #(.width(24), .enable("false")) multiplexer_1 (
    .in0(bit_extender_1_out), .in1(bit_extender_2_out), .out(multiplexer_1_out), .sel(isunsigned_1_q));
  IsUnsigned isunsigned_1 (.Opcode(opcode), .Q(isunsigned_1_q));
  Multiplexer #(.width(24), .enable("false")) multiplexer_2 (
    .in0(bit_extender_3_out), .in1(bit_extender_4_out), .out(multiplexer_2_out), .sel(isunsigned_2_q));
  IsUnsigned isunsigned_2 (.Opcode(opcode), .Q(isunsigned_2_q));
  Multiplexer #(.width(24), .enable("false")) multiplexer_3 (
    .in0(multiplexer_1_out), .in1(multiplexer_2_out), .out(multiplexer_3_out), .sel(isatype_1_q));
  IsAType isatype_1 (.Opcode(opcode), .Q(isatype_1_q));
  Multiplexer #(.width(24), .enable("false")) multiplexer_4 (
    .in0(multiplexer_3_out), .in1(bit_extender_5_out), .out(Out), .sel(isjtype_1_q));
  IsJType isjtype_1 (.Opcode(opcode), .Q(isjtype_1_q));

  // Other names for the same wires on the sheet: Op[5:0] = opcode
endmodule

// jump?
module ShouldJump (
  input  [3:0] Flags,
  input  [5:0] Opcode,
  output Q
);

  wire and_1_out, and_2_out, and_3_out, and_4_out, and_5_out, comparator_1_gt, comparator_2_lt,
       comparator_3_eq, comparator_4_eq, comparator_5_eq, comparator_6_eq;

  Comparator #(.width(6), .mode("unsigned")) comparator_1 (
    .a(Opcode), .b(6'b010100), .gt(comparator_1_gt));  // open: eq, lt
  Comparator #(.width(6), .mode("unsigned")) comparator_2 (
    .a(Opcode), .b(6'b011001), .lt(comparator_2_lt));  // open: gt, eq
  Comparator #(.width(6), .mode("unsigned")) comparator_3 (
    .a(Opcode), .b(6'b010100), .eq(comparator_3_eq));  // open: gt, lt
  Comparator #(.width(6), .mode("unsigned")) comparator_4 (
    .a(Opcode), .b(6'b010001), .eq(comparator_4_eq));  // open: gt, lt
  Comparator #(.width(6), .mode("unsigned")) comparator_5 (
    .a(Opcode), .b(6'b010010), .eq(comparator_5_eq));  // open: gt, lt
  Comparator #(.width(6), .mode("unsigned")) comparator_6 (
    .a(Opcode), .b(6'b010011), .eq(comparator_6_eq));  // open: gt, lt
  and and_1 (and_1_out, comparator_1_gt, comparator_2_lt);
  and and_2 (and_2_out, comparator_3_eq, Flags[3]);
  and and_3 (and_3_out, comparator_4_eq, Flags[2]);
  and and_4 (and_4_out, comparator_5_eq, Flags[1]);
  and and_5 (and_5_out, comparator_6_eq, Flags[0]);
  or or_1 (Q, and_1_out, and_2_out, and_3_out, and_4_out, and_5_out);

  // Other names for the same wires on the sheet: L = Flags[0]; N = Flags[1]; E = Flags[2]; G = Flags[3]
endmodule

// alusrc
module ALUSrc (
  input  [5:0] Opcode,
  output Q
);

  wire comparator_1_eq, comparator_2_eq, comparator_3_eq, comparator_4_eq, comparator_5_eq, comparator_6_eq;

  Comparator #(.width(6), .mode("unsigned")) comparator_1 (
    .a(Opcode), .b(6'b000111), .eq(comparator_1_eq));  // open: gt, lt
  Comparator #(.width(6), .mode("unsigned")) comparator_2 (
    .a(Opcode), .b(6'b001010), .eq(comparator_2_eq));  // open: gt, lt
  Comparator #(.width(6), .mode("unsigned")) comparator_3 (
    .a(Opcode), .b(6'b001100), .eq(comparator_3_eq));  // open: gt, lt
  Comparator #(.width(6), .mode("unsigned")) comparator_4 (
    .a(Opcode), .b(6'b001101), .eq(comparator_4_eq));  // open: gt, lt
  Comparator #(.width(6), .mode("unsigned")) comparator_5 (
    .a(Opcode), .b(6'b001110), .eq(comparator_5_eq));  // open: gt, lt
  Comparator #(.width(6), .mode("unsigned")) comparator_6 (
    .a(Opcode), .b(6'b010000), .eq(comparator_6_eq));  // open: gt, lt
  or or_1 (Q, comparator_1_eq, comparator_2_eq, comparator_3_eq, comparator_4_eq, comparator_5_eq, comparator_6_eq);
endmodule
