// Logisim project vpu.circ as structural Verilog: 6 circuits, main circuit VPU
module VPU (
  input  in_1,
  input  in_2,
  input  [5:0] in_3,
  input  [4:0] in_4,
  input  [4:0] in_5,
  input  [31:0] in_6,
  input  [31:0] in_7,
  input  [23:0] in_8,
  output [31:0] VRegOutHi,
  output [31:0] VRegOutLo,
  output VPUError,
  output VBus32,
  output VBus64
);

  wire and_1_out, and_2_out, and_3_out, and_4_out, and_5_out, and_6_out, is2Element, is16Bit, not_1_out,
       not_2_out, or_1_out, sv, vcfg, WriteEnable;
  wire [3:0] _4_bit_op;
  wire [4:0] origVRD, origVRS;
  wire [15:0] ALULSB, ALULSB2, ALUMSB, ALUMSB2, bit_extender_2_out, bit_extender_3_out, bit_extender_4_out,
       bit_extender_5_out, bit_extender_6_out, bit_extender_7_out, bit_extender_8_out, demultiplexer_5_out0,
       demultiplexer_5_out1, demultiplexer_6_out0, demultiplexer_6_out1, demultiplexer_7_out0,
       demultiplexer_7_out1, demultiplexer_8_out0, demultiplexer_8_out1, demultiplexer_9_out0,
       demultiplexer_9_out1, demultiplexer_10_out1, demultiplexer_11_out0, demultiplexer_11_out1,
       demultiplexer_12_out1, demultiplexer_13_out0, demultiplexer_14_out0, demultiplexer_15_out0,
       demultiplexer_16_out0, vrd_0, vrd_0____LV, vrd_0____LVI, vrd_0____LVIU, vrd_0____LVR, vrd_0____VW2BH,
       vrd_0____VW2BL, vrd_1, vrd_1____LV, vrd_1____LVR, vrd_1____VW2BH, vrd_1____VW2BL, vrd_2, vrd_2____LV,
       vrd_2____LVR, vrd_2____VW2BH, vrd_2____VW2BL, vrd_3, vrd_3____LV, vrd_3____LVR, vrd_3____vw2bh,
       vrd_3____vw2bl, VRD_LSB, VRD_LSB2, VRD_MSB, VRD_MSB_2, VRegHiLSB, VRegHiMSB, VRegLowLSB, VRegLowMSB,
       VRS_LSB, VRS_LSB2, VRS_MSB, VRS_MSB_2;
  wire [23:0] demultiplexer_4_out0, demultiplexer_4_out1;
  wire [31:0] demultiplexer_1_out0, demultiplexer_1_out1, demultiplexer_2_out0, demultiplexer_2_out1,
       demultiplexer_3_out0, multiplexer_5_out;

  BitSelector #(.width(5)) bitselector_1 (.in(origVRS), .out(is2Element), .sel(3'b001));
  Multiplexer #(.select(4), .width(16), .enable("false")) multiplexer_1 (
    .in1(vrd_0____LV), .in3(vrd_0____LVI), .in4(vrd_0____LVIU), .in5(vrd_0____LVR), .in6(vrd_0____VW2BH),
    .in7(vrd_0____VW2BL), .in8(ALULSB), .in9(ALULSB), .in10(VRS_LSB), .in11(ALULSB), .in12(ALULSB),
    .in13(ALULSB), .in14(ALULSB), .out(vrd_0), .sel(_4_bit_op));  // open: in0, in2, in15
  Multiplexer #(.select(4), .width(16), .enable("false")) multiplexer_2 (
    .in1(vrd_2____LV), .in3(vrd_0____LVI), .in4(vrd_0____LVIU), .in5(vrd_2____LVR), .in6(vrd_2____VW2BH),
    .in7(vrd_2____VW2BL), .in8(ALUMSB2), .in9(ALUMSB2), .in10(VRS_MSB_2), .in11(ALUMSB2), .in12(ALUMSB2),
    .in13(ALUMSB2), .in14(ALUMSB2), .out(vrd_2), .sel(_4_bit_op));  // open: in0, in2, in15
  Control control_1 (.vop(in_3), .EX(in_1), ._4_bit_opcode(_4_bit_op), .WriteEnable(WriteEnable), .vcfg(vcfg), .sv(sv));
  Multiplexer #(.select(4), .width(16), .enable("false")) multiplexer_3 (
    .in1(vrd_1____LV), .in3(vrd_0____LVI), .in4(vrd_0____LVIU), .in5(vrd_1____LVR), .in6(vrd_1____VW2BH),
    .in7(vrd_1____VW2BL), .in8(ALULSB2), .in9(ALULSB2), .in10(VRS_LSB2), .in11(ALULSB2), .in12(ALULSB2),
    .in13(ALULSB2), .in14(ALULSB2), .out(vrd_1), .sel(_4_bit_op));  // open: in0, in2, in15
  RegFile regfile_1 (
    .MSB(vrd_3), .VRD(in_4), .MSB2(vrd_2), .LSB2(vrd_1), .VRS(in_5), .LSB(vrd_0), .vcfg(vcfg), .Clock(in_2),
    .WriteEnable(WriteEnable), .vop(in_3), .MSB_2(VRD_MSB), .MSB2_2(VRD_MSB_2), .LSB2_2(VRD_LSB2),
    .LSB_2(VRD_LSB), .MSB_minus(VRS_MSB), .MSB2_minus(VRS_MSB_2), .LSB2_minus(VRS_LSB2), .LSB_minus(VRS_LSB),
    .is16Bit(is16Bit), .origVRS(origVRS), .origVRD(origVRD));
  Demultiplexer #(.width(32), .enable("false")) demultiplexer_1 (
    .out0(demultiplexer_1_out0), .out1(demultiplexer_1_out1), .in(in_6), .sel(is16Bit));
  Multiplexer #(.select(4), .width(16), .enable("false")) multiplexer_4 (
    .in1(vrd_3____LV), .in3(vrd_0____LVI), .in4(vrd_0____LVIU), .in5(vrd_3____LVR), .in6(vrd_3____vw2bh),
    .in7(vrd_3____vw2bl), .in8(ALUMSB), .in9(ALUMSB), .in10(VRS_MSB), .in11(ALUMSB), .in12(ALUMSB),
    .in13(ALUMSB), .in14(ALUMSB), .out(vrd_3), .sel(_4_bit_op));  // open: in0, in2, in15
  Demultiplexer #(.width(32), .enable("false")) demultiplexer_2 (
    .out0(demultiplexer_2_out0), .out1(demultiplexer_2_out1), .in(demultiplexer_1_out0), .sel(is2Element));
  Demultiplexer #(.width(32), .enable("false")) demultiplexer_3 (
    .out0(demultiplexer_3_out0), .in(demultiplexer_1_out1), .sel(is2Element));  // open: out1
  assign vrd_0____LVI = {{11{in_5[4]}}, in_5};  // Bit_Extender bit_extender_1
  Demultiplexer #(.width(24), .enable("false")) demultiplexer_4 (
    .out0(demultiplexer_4_out0), .out1(demultiplexer_4_out1), .in(in_8), .sel(is16Bit));
  Multiplexer #(.width(32), .enable("false")) multiplexer_5 (
    .in0(in_7), .in1(in_6), .out(multiplexer_5_out), .sel(and_1_out));
  and and_1 (and_1_out, is16Bit, is2Element);
  assign bit_extender_2_out = {{8{demultiplexer_4_out0[7]}}, demultiplexer_4_out0[7:0]};  // Bit_Extender bit_extender_2
  assign bit_extender_3_out = {{8{demultiplexer_2_out0[7]}}, demultiplexer_2_out0[7:0]};  // Bit_Extender bit_extender_3
  assign bit_extender_4_out = {{8{demultiplexer_2_out0[15]}}, demultiplexer_2_out0[15:8]};  // Bit_Extender bit_extender_4
  assign bit_extender_5_out = {{8{demultiplexer_2_out0[23]}}, demultiplexer_2_out0[23:16]};  // Bit_Extender bit_extender_5
  assign bit_extender_6_out = {{8{demultiplexer_2_out0[31]}}, demultiplexer_2_out0[31:24]};  // Bit_Extender bit_extender_6
  assign bit_extender_7_out = {{8{demultiplexer_2_out1[23]}}, demultiplexer_2_out1[23:16]};  // Bit_Extender bit_extender_7
  assign bit_extender_8_out = {{8{demultiplexer_2_out1[31]}}, demultiplexer_2_out1[31:24]};  // Bit_Extender bit_extender_8
  assign vrd_0____LVIU = {{11{1'b0}}, in_5};  // Bit_Extender bit_extender_9
  Multiplexer #(.width(16), .enable("false")) multiplexer_6 (
    .in0(bit_extender_2_out), .in1(demultiplexer_4_out1[15:0]), .out(vrd_0____LVR), .sel(is16Bit));
  Multiplexer #(.width(16), .enable("false")) multiplexer_7 (
    .in0(bit_extender_2_out), .in1(demultiplexer_4_out1[15:0]), .out(vrd_1____LVR), .sel(is16Bit));
  Multiplexer #(.width(16), .enable("false")) multiplexer_8 (
    .in0(bit_extender_2_out), .in1(demultiplexer_4_out1[15:0]), .out(vrd_2____LVR), .sel(is16Bit));
  Multiplexer #(.width(16), .enable("false")) multiplexer_9 (
    .in0(bit_extender_2_out), .in1(demultiplexer_4_out1[15:0]), .out(vrd_3____LVR), .sel(is16Bit));
  Multiplexer #(.select(2), .width(16), .enable("false")) multiplexer_10 (
    .in0(bit_extender_3_out), .in1(bit_extender_7_out), .in2(multiplexer_5_out[15:0]),
    .in3(multiplexer_5_out[15:0]), .out(vrd_0____LV), .sel({is16Bit, is2Element}));
  Multiplexer #(.select(2), .width(16), .enable("false")) multiplexer_11 (
    .in0(bit_extender_4_out), .in1(bit_extender_8_out), .in2(multiplexer_5_out[31:16]),
    .in3(multiplexer_5_out[31:16]), .out(vrd_1____LV), .sel({is16Bit, is2Element}));
  Multiplexer #(.width(16), .enable("false")) multiplexer_12 (
    .in0(bit_extender_5_out), .in1(demultiplexer_3_out0[15:0]), .out(vrd_2____LV), .sel(is16Bit));
  Multiplexer #(.width(16), .enable("false")) multiplexer_13 (
    .in0(bit_extender_6_out), .in1(demultiplexer_3_out0[31:16]), .out(vrd_3____LV), .sel(is16Bit));
  ALU alu_1 (
    .Input_1(VRD_MSB), .Input_1_2(VRD_MSB_2), .Input_1_3(VRD_LSB2), .Input_1_4(VRD_LSB), .Input_2(VRS_MSB),
    .Input_2_2(VRS_MSB_2), .Input_2_3(VRS_LSB2), .Input_2_4(VRS_LSB), .opcode(_4_bit_op), .Output(ALUMSB),
    .Output_2(ALUMSB2), .Output_3(ALULSB2), .Output_4(ALULSB));
  assign vrd_0____VW2BH = {{8{VRS_LSB[15]}}, VRS_LSB[15:8]};  // Bit_Extender bit_extender_10
  assign vrd_1____VW2BH = {{8{VRS_LSB2[15]}}, VRS_LSB2[15:8]};  // Bit_Extender bit_extender_11
  assign vrd_2____VW2BH = {{8{VRS_MSB_2[15]}}, VRS_MSB_2[15:8]};  // Bit_Extender bit_extender_12
  assign vrd_3____vw2bh = {{8{VRS_MSB[15]}}, VRS_MSB[15:8]};  // Bit_Extender bit_extender_13
  Demultiplexer #(.width(16), .enable("false")) demultiplexer_5 (
    .out0(demultiplexer_5_out0), .out1(demultiplexer_5_out1), .in(VRD_LSB), .sel(is16Bit));
  Demultiplexer #(.width(16), .enable("false")) demultiplexer_6 (
    .out0(demultiplexer_6_out0), .out1(demultiplexer_6_out1), .in(VRD_LSB2), .sel(is16Bit));
  Demultiplexer #(.width(16), .enable("false")) demultiplexer_7 (
    .out0(demultiplexer_7_out0), .out1(demultiplexer_7_out1), .in(VRD_MSB_2), .sel(is16Bit));
  Demultiplexer #(.width(16), .enable("false")) demultiplexer_8 (
    .out0(demultiplexer_8_out0), .out1(demultiplexer_8_out1), .in(VRD_MSB), .sel(is16Bit));
  Demultiplexer #(.width(16), .enable("false")) demultiplexer_9 (
    .out0(demultiplexer_9_out0), .out1(demultiplexer_9_out1), .in(demultiplexer_5_out0), .sel(is2Element));
  Demultiplexer #(.width(16), .enable("false")) demultiplexer_10 (
    .out0(VRegLowLSB), .out1(demultiplexer_10_out1), .in(demultiplexer_5_out1), .sel(is2Element));
  Demultiplexer #(.width(16), .enable("false")) demultiplexer_11 (
    .out0(demultiplexer_11_out0), .out1(demultiplexer_11_out1), .in(demultiplexer_6_out0), .sel(is2Element));
  Demultiplexer #(.width(16), .enable("false")) demultiplexer_12 (
    .out0(VRegLowMSB), .out1(demultiplexer_12_out1), .in(demultiplexer_6_out1), .sel(is2Element));
  Demultiplexer #(.width(16), .enable("false")) demultiplexer_13 (
    .out0(demultiplexer_13_out0), .in(demultiplexer_7_out0), .sel(is2Element));  // open: out1
  Demultiplexer #(.width(16), .enable("false")) demultiplexer_14 (
    .out0(demultiplexer_14_out0), .in(demultiplexer_7_out1), .sel(is2Element));  // open: out1
  Demultiplexer #(.width(16), .enable("false")) demultiplexer_15 (
    .out0(demultiplexer_15_out0), .in(demultiplexer_8_out0), .sel(is2Element));  // open: out1
  Demultiplexer #(.width(16), .enable("false")) demultiplexer_16 (
    .out0(demultiplexer_16_out0), .in(demultiplexer_8_out1), .sel(is2Element));  // open: out1
  assign vrd_0____VW2BL = {{8{VRS_LSB[7]}}, VRS_LSB[7:0]};  // Bit_Extender bit_extender_14
  assign vrd_1____VW2BL = {{8{VRS_LSB2[7]}}, VRS_LSB2[7:0]};  // Bit_Extender bit_extender_15
  assign vrd_2____VW2BL = {{8{VRS_MSB_2[7]}}, VRS_MSB_2[7:0]};  // Bit_Extender bit_extender_16
  assign vrd_3____vw2bl = {{8{VRS_MSB[7]}}, VRS_MSB[7:0]};  // Bit_Extender bit_extender_17
  Multiplexer #(.select(2), .width(16), .enable("false")) multiplexer_14 (
    .in0({demultiplexer_15_out0[7:0], demultiplexer_13_out0[7:0]}),
    .in1({demultiplexer_11_out1[7:0], demultiplexer_9_out1[7:0]}), .in2(demultiplexer_16_out0),
    .in3(demultiplexer_12_out1), .out(VRegHiMSB), .sel({is16Bit, is2Element}));
  Multiplexer #(.select(2), .width(16), .enable("false")) multiplexer_15 (
    .in0({demultiplexer_11_out0[7:0], demultiplexer_9_out0[7:0]}), .in2(demultiplexer_14_out0),
    .in3(demultiplexer_10_out1), .out(VRegHiLSB), .sel({is16Bit, is2Element}));  // open: in1
  not not_1 (not_1_out, is16Bit);
  not not_2 (not_2_out, is2Element);
  Multiplexer #(.width(32), .enable("false")) multiplexer_16 (
    .in0({32{1'b0}}), .in1({VRegHiMSB, VRegHiLSB}), .out(VRegOutHi), .sel(sv));
  Multiplexer #(.width(32), .enable("false")) multiplexer_17 (
    .in0({32{1'b0}}), .in1({VRegLowMSB, VRegLowLSB}), .out(VRegOutLo), .sel(sv));
  and and_2 (and_2_out, not_1_out, not_2_out);
  or or_1 (or_1_out, and_2_out, and_3_out);
  and and_3 (and_3_out, is16Bit, is2Element);
  and and_4 (and_4_out, is16Bit, not_2_out);
  Multiplexer #(.enable("false")) multiplexer_18 (.in0(1'b0), .in1(or_1_out), .out(VBus32), .sel(and_5_out));
  and and_5 (and_5_out, sv, in_1);
  Multiplexer #(.enable("false")) multiplexer_19 (.in0(1'b0), .in1(and_4_out), .out(VBus64), .sel(and_6_out));
  and and_6 (and_6_out, sv, in_1);

  assign VPUError = 1'b0;

  // Other names for the same wires on the sheet: CLK = in_2; EX = in_1; RAMOutHi[31:0] = in_6; RAMOutLo[31:0] = in_7;
  //   RegOut2[23:0] = in_8; vop[5:0] = in_3; vrd[4:0] = in_4; vrd_1____LVI[15:0] = vrd_0____LVI;
  //   vrd_2____LVI[15:0] = vrd_0____LVI; vrd_3____LVI[15:0] = vrd_0____LVI; vrd_1____LVIU[15:0] = vrd_0____LVIU;
  //   vrd_2____LVIU[15:0] = vrd_0____LVIU; vrd_3____LVIU[15:0] = vrd_0____LVIU;
  //   VRegOutHi_t[31:0] = {VRegHiMSB, VRegHiLSB}; VRegOutLo_t[31:0] = {VRegLowMSB, VRegLowLSB}; vrs[4:0] = in_5

  // Notes on the sheet:
  //   lvi
  //   lvr
  //   Load Vector Instruc
  //   lviu
  //   vw2bh
  //   vw2bl
  //   Store Vector Instruc
endmodule

module RegRow (
  input  [15:0] MSB,
  input  [15:0] MSB2,
  input  [15:0] LSB2,
  input  [15:0] LSB,
  input  [4:0] VRS,
  input  Clock,
  input  Write_Enable,
  output [15:0] MSB_2,
  output [15:0] MSB2_2,
  output [15:0] LSB2_2,
  output [15:0] LSB_2
);

  wire and_1_out, and_2_out, or_1_out;
  wire [15:0] demultiplexer_1_out1, demultiplexer_2_out1, multiplexer_1_out, multiplexer_2_out, Out1, Out2,
       Out3, Out4;

  Multiplexer #(.width(16), .enable("false")) multiplexer_1 (
    .in0(MSB), .in1(LSB2), .out(multiplexer_1_out), .sel(VRS[1]));
  Multiplexer #(.width(16), .enable("false")) multiplexer_2 (
    .in0(MSB2), .in1(LSB), .out(multiplexer_2_out), .sel(VRS[1]));
  and and_1 (and_1_out, or_1_out, Write_Enable);
  or or_1 (or_1_out, VRS[1], VRS[2]);
  Register #(.width(16)) Reg_1 (.D(multiplexer_1_out), .en(and_1_out), .Q(Out1), .clk(Clock));  // open: clr
  Register #(.width(16)) Reg_2 (.D(multiplexer_2_out), .en(and_1_out), .Q(Out2), .clk(Clock));  // open: clr
  and and_2 (and_2_out, Write_Enable, VRS[2]);
  Register #(.width(16)) Reg_3 (.D(LSB2), .en(and_2_out), .Q(Out3), .clk(Clock));  // open: clr
  Demultiplexer #(.width(16), .enable("false")) demultiplexer_1 (
    .out0(MSB_2), .out1(demultiplexer_1_out1), .in(Out1), .sel(VRS[1]));
  Demultiplexer #(.width(16), .enable("false")) demultiplexer_2 (
    .out0(MSB2_2), .out1(demultiplexer_2_out1), .in(Out2), .sel(VRS[1]));
  Register #(.width(16)) Reg_4 (.D(LSB), .en(and_2_out), .Q(Out4), .clk(Clock));  // open: clr
  Multiplexer #(.width(16), .enable("false")) multiplexer_3 (
    .in0(Out3), .in1(demultiplexer_1_out1), .out(LSB2_2), .sel(VRS[1]));
  Multiplexer #(.width(16), .enable("false")) multiplexer_4 (
    .in0(Out4), .in1(demultiplexer_2_out1), .out(LSB_2), .sel(VRS[1]));

  // Other names for the same wires on the sheet: CLK = Clock

  // Notes on the sheet:
  //   4 element vector
  //   MSB = vrd[3] = reg1
  //   MSB2 = vrd[2] = reg2
  //   LSB2 = vrd[1] = reg3
  //   LSB = vrd[0] = reg4
  //   2 element vector
  //   LSB2 = vrd[1] = reg1
  //   LSB = vrd[0] = reg2
endmodule

module RegFile (
  input  [15:0] MSB,
  input  [4:0] VRD,
  input  [15:0] MSB2,
  input  [15:0] LSB2,
  input  [4:0] VRS,
  input  [15:0] LSB,
  input  vcfg,
  input  Clock,
  input  WriteEnable,
  input  [5:0] vop,
  output [15:0] MSB_2,
  output [15:0] MSB2_2,
  output [15:0] LSB2_2,
  output [15:0] LSB_2,
  output [15:0] MSB_minus,
  output is16Bit,
  output [15:0] MSB2_minus,
  output [4:0] origVRS,
  output [4:0] origVRD,
  output [15:0] LSB2_minus,
  output [15:0] LSB_minus
);

  wire and_1_out, comparator_1_eq, comparator_1_gt, or_1_out, WE1, WE2, WE3, WE4, WE5, WE6, WE7, WE8, WE9,
       WE10, WE11, WE12, WE13, WE14, WE15, WE16, WE17, WE18, WE19, WE20, WE21, WE22, WE23, WE24, WE25, WE26,
       WE27, WE28, WE29, WE30, WE31, WE32;
  wire [15:0] OTLSB2_1, OTLSB2_2, OTLSB2_3, OTLSB2_4, OTLSB2_5, OTLSB2_6, OTLSB2_7, OTLSB2_8, OTLSB2_9,
       OTLSB2_10, OTLSB2_11, OTLSB2_12, OTLSB2_13, OTLSB2_14, OTLSB2_15, OTLSB2_16, OTLSB2_17, OTLSB2_18,
       OTLSB2_19, OTLSB2_20, OTLSB2_21, OTLSB2_22, OTLSB2_23, OTLSB2_24, OTLSB2_25, OTLSB2_26, OTLSB2_27,
       OTLSB2_28, OTLSB2_29, OTLSB2_30, OTLSB2_31, OTLSB2_32, OTLSB_1, OTLSB_2, OTLSB_3, OTLSB_4, OTLSB_5,
       OTLSB_6, OTLSB_7, OTLSB_8, OTLSB_9, OTLSB_10, OTLSB_11, OTLSB_12, OTLSB_13, OTLSB_14, OTLSB_15,
       OTLSB_16, OTLSB_17, OTLSB_18, OTLSB_19, OTLSB_20, OTLSB_21, OTLSB_22, OTLSB_23, OTLSB_24, OTLSB_25,
       OTLSB_26, OTLSB_27, OTLSB_28, OTLSB_29, OTLSB_30, OTLSB_31, OTLSB_32, OTMSB2_1, OTMSB2_2, OTMSB2_3,
       OTMSB2_4, OTMSB2_5, OTMSB2_6, OTMSB2_7, OTMSB2_8, OTMSB2_9, OTMSB2_10, OTMSB2_11, OTMSB2_12,
       OTMSB2_13, OTMSB2_14, OTMSB2_15, OTMSB2_16, OTMSB2_17, OTMSB2_18, OTMSB2_19, OTMSB2_20, OTMSB2_21,
       OTMSB2_22, OTMSB2_23, OTMSB2_24, OTMSB2_25, OTMSB2_26, OTMSB2_27, OTMSB2_28, OTMSB2_29, OTMSB2_30,
       OTMSB2_31, OTMSB2_32, OTMSB_1, OTMSB_2, OTMSB_3, OTMSB_4, OTMSB_5, OTMSB_6, OTMSB_7, OTMSB_8, OTMSB_9,
       OTMSB_10, OTMSB_11, OTMSB_12, OTMSB_13, OTMSB_14, OTMSB_15, OTMSB_16, OTMSB_17, OTMSB_18, OTMSB_19,
       OTMSB_20, OTMSB_21, OTMSB_22, OTMSB_23, OTMSB_24, OTMSB_25, OTMSB_26, OTMSB_27, OTMSB_28, OTMSB_29,
       OTMSB_30, OTMSB_31, OTMSB_32;

  Demultiplexer #(.select(5), .enable("false")) demultiplexer_1 (
    .out0(WE1), .out1(WE2), .out2(WE3), .out3(WE4), .out4(WE5), .out5(WE6), .out6(WE7), .out7(WE8),
    .out8(WE9), .out9(WE10), .out10(WE11), .out11(WE12), .out12(WE13), .out13(WE14), .out14(WE15),
    .out15(WE16), .out16(WE17), .out17(WE18), .out18(WE19), .out19(WE20), .out20(WE21), .out21(WE22),
    .out22(WE23), .out23(WE24), .out24(WE25), .out25(WE26), .out26(WE27), .out27(WE28), .out28(WE29),
    .out29(WE30), .out30(WE31), .out31(WE32), .in(WriteEnable), .sel(VRD));
  Register #(.width(5)) u_VRD (.D(VRD), .en(vcfg), .Q(origVRD), .clk(Clock));  // open: clr
  Register #(.width(5)) u_VRS (.D(VRS), .en(vcfg), .Q(origVRS), .clk(Clock));  // open: clr
  RegRow regrow_1 (
    .MSB(MSB), .MSB2(MSB2), .LSB2(LSB2), .LSB(LSB), .VRS(origVRS), .MSB_2(OTMSB_17), .MSB2_2(OTMSB2_17),
    .LSB2_2(OTLSB2_17), .LSB_2(OTLSB_17), .Clock(Clock), .Write_Enable(WE17));
  RegRow regrow_2 (
    .MSB(MSB), .MSB2(MSB2), .LSB2(LSB2), .LSB(LSB), .VRS(origVRS), .MSB_2(OTMSB_21), .MSB2_2(OTMSB2_21),
    .LSB2_2(OTLSB2_21), .LSB_2(OTLSB_21), .Clock(Clock), .Write_Enable(WE21));
  RegRow regrow_3 (
    .MSB(MSB), .MSB2(MSB2), .LSB2(LSB2), .LSB(LSB), .VRS(origVRS), .MSB_2(OTMSB_25), .MSB2_2(OTMSB2_25),
    .LSB2_2(OTLSB2_25), .LSB_2(OTLSB_25), .Clock(Clock), .Write_Enable(WE25));
  RegRow regrow_4 (
    .MSB(MSB), .MSB2(MSB2), .LSB2(LSB2), .LSB(LSB), .VRS(origVRS), .MSB_2(OTMSB_29), .MSB2_2(OTMSB2_29),
    .LSB2_2(OTLSB2_29), .LSB_2(OTLSB_29), .Clock(Clock), .Write_Enable(WE29));
  RegRow regrow_5 (
    .MSB(MSB), .MSB2(MSB2), .LSB2(LSB2), .LSB(LSB), .VRS(origVRS), .MSB_2(OTMSB_1), .MSB2_2(OTMSB2_1),
    .LSB2_2(OTLSB2_1), .LSB_2(OTLSB_1), .Clock(Clock), .Write_Enable(WE1));
  RegRow regrow_6 (
    .MSB(MSB), .MSB2(MSB2), .LSB2(LSB2), .LSB(LSB), .VRS(origVRS), .MSB_2(OTMSB_5), .MSB2_2(OTMSB2_5),
    .LSB2_2(OTLSB2_5), .LSB_2(OTLSB_5), .Clock(Clock), .Write_Enable(WE5));
  RegRow regrow_7 (
    .MSB(MSB), .MSB2(MSB2), .LSB2(LSB2), .LSB(LSB), .VRS(origVRS), .MSB_2(OTMSB_9), .MSB2_2(OTMSB2_9),
    .LSB2_2(OTLSB2_9), .LSB_2(OTLSB_9), .Clock(Clock), .Write_Enable(WE9));
  RegRow regrow_8 (
    .MSB(MSB), .MSB2(MSB2), .LSB2(LSB2), .LSB(LSB), .VRS(origVRS), .MSB_2(OTMSB_13), .MSB2_2(OTMSB2_13),
    .LSB2_2(OTLSB2_13), .LSB_2(OTLSB_13), .Clock(Clock), .Write_Enable(WE13));
  or or_1 (or_1_out, comparator_1_gt, comparator_1_eq);
  Comparator #(.width(5), .mode("unsigned")) comparator_1 (
    .a(VRD), .b(origVRD), .gt(comparator_1_gt), .eq(comparator_1_eq));  // open: lt
  RegRow regrow_9 (
    .MSB(MSB), .MSB2(MSB2), .LSB2(LSB2), .LSB(LSB), .VRS(origVRS), .MSB_2(OTMSB_30), .MSB2_2(OTMSB2_30),
    .LSB2_2(OTLSB2_30), .LSB_2(OTLSB_30), .Clock(Clock), .Write_Enable(WE30));
  RegRow regrow_10 (
    .MSB(MSB), .MSB2(MSB2), .LSB2(LSB2), .LSB(LSB), .VRS(origVRS), .MSB_2(OTMSB_2), .MSB2_2(OTMSB2_2),
    .LSB2_2(OTLSB2_2), .LSB_2(OTLSB_2), .Clock(Clock), .Write_Enable(WE2));
  RegRow regrow_11 (
    .MSB(MSB), .MSB2(MSB2), .LSB2(LSB2), .LSB(LSB), .VRS(origVRS), .MSB_2(OTMSB_6), .MSB2_2(OTMSB2_6),
    .LSB2_2(OTLSB2_6), .LSB_2(OTLSB_6), .Clock(Clock), .Write_Enable(WE6));
  RegRow regrow_12 (
    .MSB(MSB), .MSB2(MSB2), .LSB2(LSB2), .LSB(LSB), .VRS(origVRS), .MSB_2(OTMSB_10), .MSB2_2(OTMSB2_10),
    .LSB2_2(OTLSB2_10), .LSB_2(OTLSB_10), .Clock(Clock), .Write_Enable(WE10));
  RegRow regrow_13 (
    .MSB(MSB), .MSB2(MSB2), .LSB2(LSB2), .LSB(LSB), .VRS(origVRS), .MSB_2(OTMSB_14), .MSB2_2(OTMSB2_14),
    .LSB2_2(OTLSB2_14), .LSB_2(OTLSB_14), .Clock(Clock), .Write_Enable(WE14));
  RegRow regrow_14 (
    .MSB(MSB), .MSB2(MSB2), .LSB2(LSB2), .LSB(LSB), .VRS(origVRS), .MSB_2(OTMSB_18), .MSB2_2(OTMSB2_18),
    .LSB2_2(OTLSB2_18), .LSB_2(OTLSB_18), .Clock(Clock), .Write_Enable(WE18));
  RegRow regrow_15 (
    .MSB(MSB), .MSB2(MSB2), .LSB2(LSB2), .LSB(LSB), .VRS(origVRS), .MSB_2(OTMSB_22), .MSB2_2(OTMSB2_22),
    .LSB2_2(OTLSB2_22), .LSB_2(OTLSB_22), .Clock(Clock), .Write_Enable(WE22));
  RegRow regrow_16 (
    .MSB(MSB), .MSB2(MSB2), .LSB2(LSB2), .LSB(LSB), .VRS(origVRS), .MSB_2(OTMSB_26), .MSB2_2(OTMSB2_26),
    .LSB2_2(OTLSB2_26), .LSB_2(OTLSB_26), .Clock(Clock), .Write_Enable(WE26));
  and and_1 (and_1_out, or_1_out, vop[5]);
  not not_1 (is16Bit, and_1_out);
  RegRow regrow_17 (
    .MSB(MSB), .MSB2(MSB2), .LSB2(LSB2), .LSB(LSB), .VRS(origVRS), .MSB_2(OTMSB_19), .MSB2_2(OTMSB2_19),
    .LSB2_2(OTLSB2_19), .LSB_2(OTLSB_19), .Clock(Clock), .Write_Enable(WE19));
  RegRow regrow_18 (
    .MSB(MSB), .MSB2(MSB2), .LSB2(LSB2), .LSB(LSB), .VRS(origVRS), .MSB_2(OTMSB_23), .MSB2_2(OTMSB2_23),
    .LSB2_2(OTLSB2_23), .LSB_2(OTLSB_23), .Clock(Clock), .Write_Enable(WE23));
  RegRow regrow_19 (
    .MSB(MSB), .MSB2(MSB2), .LSB2(LSB2), .LSB(LSB), .VRS(origVRS), .MSB_2(OTMSB_27), .MSB2_2(OTMSB2_27),
    .LSB2_2(OTLSB2_27), .LSB_2(OTLSB_27), .Clock(Clock), .Write_Enable(WE27));
  RegRow regrow_20 (
    .MSB(MSB), .MSB2(MSB2), .LSB2(LSB2), .LSB(LSB), .VRS(origVRS), .MSB_2(OTMSB_31), .MSB2_2(OTMSB2_31),
    .LSB2_2(OTLSB2_31), .LSB_2(OTLSB_31), .Clock(Clock), .Write_Enable(WE31));
  RegRow regrow_21 (
    .MSB(MSB), .MSB2(MSB2), .LSB2(LSB2), .LSB(LSB), .VRS(origVRS), .MSB_2(OTMSB_3), .MSB2_2(OTMSB2_3),
    .LSB2_2(OTLSB2_3), .LSB_2(OTLSB_3), .Clock(Clock), .Write_Enable(WE3));
  RegRow regrow_22 (
    .MSB(MSB), .MSB2(MSB2), .LSB2(LSB2), .LSB(LSB), .VRS(origVRS), .MSB_2(OTMSB_7), .MSB2_2(OTMSB2_7),
    .LSB2_2(OTLSB2_7), .LSB_2(OTLSB_7), .Clock(Clock), .Write_Enable(WE7));
  RegRow regrow_23 (
    .MSB(MSB), .MSB2(MSB2), .LSB2(LSB2), .LSB(LSB), .VRS(origVRS), .MSB_2(OTMSB_11), .MSB2_2(OTMSB2_11),
    .LSB2_2(OTLSB2_11), .LSB_2(OTLSB_11), .Clock(Clock), .Write_Enable(WE11));
  RegRow regrow_24 (
    .MSB(MSB), .MSB2(MSB2), .LSB2(LSB2), .LSB(LSB), .VRS(origVRS), .MSB_2(OTMSB_15), .MSB2_2(OTMSB2_15),
    .LSB2_2(OTLSB2_15), .LSB_2(OTLSB_15), .Clock(Clock), .Write_Enable(WE15));
  RegRow regrow_25 (
    .MSB(MSB), .MSB2(MSB2), .LSB2(LSB2), .LSB(LSB), .VRS(origVRS), .MSB_2(OTMSB_4), .MSB2_2(OTMSB2_4),
    .LSB2_2(OTLSB2_4), .LSB_2(OTLSB_4), .Clock(Clock), .Write_Enable(WE4));
  RegRow regrow_26 (
    .MSB(MSB), .MSB2(MSB2), .LSB2(LSB2), .LSB(LSB), .VRS(origVRS), .MSB_2(OTMSB_8), .MSB2_2(OTMSB2_8),
    .LSB2_2(OTLSB2_8), .LSB_2(OTLSB_8), .Clock(Clock), .Write_Enable(WE8));
  RegRow regrow_27 (
    .MSB(MSB), .MSB2(MSB2), .LSB2(LSB2), .LSB(LSB), .VRS(origVRS), .MSB_2(OTMSB_12), .MSB2_2(OTMSB2_12),
    .LSB2_2(OTLSB2_12), .LSB_2(OTLSB_12), .Clock(Clock), .Write_Enable(WE12));
  RegRow regrow_28 (
    .MSB(MSB), .MSB2(MSB2), .LSB2(LSB2), .LSB(LSB), .VRS(origVRS), .MSB_2(OTMSB_16), .MSB2_2(OTMSB2_16),
    .LSB2_2(OTLSB2_16), .LSB_2(OTLSB_16), .Clock(Clock), .Write_Enable(WE16));
  RegRow regrow_29 (
    .MSB(MSB), .MSB2(MSB2), .LSB2(LSB2), .LSB(LSB), .VRS(origVRS), .MSB_2(OTMSB_20), .MSB2_2(OTMSB2_20),
    .LSB2_2(OTLSB2_20), .LSB_2(OTLSB_20), .Clock(Clock), .Write_Enable(WE20));
  RegRow regrow_30 (
    .MSB(MSB), .MSB2(MSB2), .LSB2(LSB2), .LSB(LSB), .VRS(origVRS), .MSB_2(OTMSB_24), .MSB2_2(OTMSB2_24),
    .LSB2_2(OTLSB2_24), .LSB_2(OTLSB_24), .Clock(Clock), .Write_Enable(WE24));
  RegRow regrow_31 (
    .MSB(MSB), .MSB2(MSB2), .LSB2(LSB2), .LSB(LSB), .VRS(origVRS), .MSB_2(OTMSB_28), .MSB2_2(OTMSB2_28),
    .LSB2_2(OTLSB2_28), .LSB_2(OTLSB_28), .Clock(Clock), .Write_Enable(WE28));
  RegRow regrow_32 (
    .MSB(MSB), .MSB2(MSB2), .LSB2(LSB2), .LSB(LSB), .VRS(origVRS), .MSB_2(OTMSB_32), .MSB2_2(OTMSB2_32),
    .LSB2_2(OTLSB2_32), .LSB_2(OTLSB_32), .Clock(Clock), .Write_Enable(WE32));
  Multiplexer #(.select(5), .width(16), .enable("false")) multiplexer_1 (
    .in0(OTMSB_1), .in1(OTMSB_2), .in2(OTMSB_3), .in3(OTMSB_4), .in4(OTMSB_5), .in5(OTMSB_6), .in6(OTMSB_7),
    .in7(OTMSB_8), .in8(OTMSB_9), .in9(OTMSB_10), .in10(OTMSB_11), .in11(OTMSB_12), .in12(OTMSB_13),
    .in13(OTMSB_14), .in14(OTMSB_15), .in15(OTMSB_16), .in16(OTMSB_17), .in17(OTMSB_18), .in18(OTMSB_19),
    .in19(OTMSB_20), .in20(OTMSB_21), .in21(OTMSB_22), .in22(OTMSB_23), .in23(OTMSB_24), .in24(OTMSB_25),
    .in25(OTMSB_26), .in26(OTMSB_27), .in27(OTMSB_28), .in28(OTMSB_29), .in29(OTMSB_30), .in30(OTMSB_31),
    .in31(OTMSB_32), .out(MSB_2), .sel(VRD));
  Multiplexer #(.select(5), .width(16), .enable("false")) multiplexer_2 (
    .in0(OTLSB_1), .in1(OTLSB_2), .in2(OTLSB_3), .in3(OTLSB_4), .in4(OTLSB_5), .in5(OTLSB_6), .in6(OTLSB_7),
    .in7(OTLSB_8), .in8(OTLSB_9), .in9(OTLSB_10), .in10(OTLSB_11), .in11(OTLSB_12), .in12(OTLSB_13),
    .in13(OTLSB_14), .in14(OTLSB_15), .in15(OTLSB_16), .in16(OTLSB_17), .in17(OTLSB_18), .in18(OTLSB_19),
    .in19(OTLSB_20), .in20(OTLSB_21), .in21(OTLSB_22), .in22(OTLSB_23), .in23(OTLSB_24), .in24(OTLSB_25),
    .in25(OTLSB_26), .in26(OTLSB_27), .in27(OTLSB_28), .in28(OTLSB_29), .in29(OTLSB_30), .in30(OTLSB_31),
    .in31(OTLSB_32), .out(LSB_2), .sel(VRD));
  Multiplexer #(.select(5), .width(16), .enable("false")) multiplexer_3 (
    .in0(OTMSB2_1), .in1(OTMSB2_2), .in2(OTMSB2_3), .in3(OTMSB2_4), .in4(OTMSB2_5), .in5(OTMSB2_6),
    .in6(OTMSB2_7), .in7(OTMSB2_8), .in8(OTMSB2_9), .in9(OTMSB2_10), .in10(OTMSB2_11), .in11(OTMSB2_12),
    .in12(OTMSB2_13), .in13(OTMSB2_14), .in14(OTMSB2_15), .in15(OTMSB2_16), .in16(OTMSB2_17),
    .in17(OTMSB2_18), .in18(OTMSB2_19), .in19(OTMSB2_20), .in20(OTMSB2_21), .in21(OTMSB2_22),
    .in22(OTMSB2_23), .in23(OTMSB2_24), .in24(OTMSB2_25), .in25(OTMSB2_26), .in26(OTMSB2_27),
    .in27(OTMSB2_28), .in28(OTMSB2_29), .in29(OTMSB2_30), .in30(OTMSB2_31), .in31(OTMSB2_32), .out(MSB2_2),
    .sel(VRD));
  Multiplexer #(.select(5), .width(16), .enable("false")) multiplexer_4 (
    .in0(OTLSB2_1), .in1(OTLSB2_2), .in2(OTLSB2_3), .in3(OTLSB2_4), .in4(OTLSB2_5), .in5(OTLSB2_6),
    .in6(OTLSB2_7), .in7(OTLSB2_8), .in8(OTLSB2_9), .in9(OTLSB2_10), .in10(OTLSB2_11), .in11(OTLSB2_12),
    .in12(OTLSB2_13), .in13(OTLSB2_14), .in14(OTLSB2_15), .in15(OTLSB2_16), .in16(OTLSB2_17),
    .in17(OTLSB2_18), .in18(OTLSB2_19), .in19(OTLSB2_20), .in20(OTLSB2_21), .in21(OTLSB2_22),
    .in22(OTLSB2_23), .in23(OTLSB2_24), .in24(OTLSB2_25), .in25(OTLSB2_26), .in26(OTLSB2_27),
    .in27(OTLSB2_28), .in28(OTLSB2_29), .in29(OTLSB2_30), .in30(OTLSB2_31), .in31(OTLSB2_32), .out(LSB2_2),
    .sel(VRD));
  Multiplexer #(.select(5), .width(16), .enable("false")) multiplexer_5 (
    .in0(OTMSB_1), .in1(OTMSB_2), .in2(OTMSB_3), .in3(OTMSB_4), .in4(OTMSB_5), .in5(OTMSB_6), .in6(OTMSB_7),
    .in7(OTMSB_8), .in8(OTMSB_9), .in9(OTMSB_10), .in10(OTMSB_11), .in11(OTMSB_12), .in12(OTMSB_13),
    .in13(OTMSB_14), .in14(OTMSB_15), .in15(OTMSB_16), .in16(OTMSB_17), .in17(OTMSB_18), .in18(OTMSB_19),
    .in19(OTMSB_20), .in20(OTMSB_21), .in21(OTMSB_22), .in22(OTMSB_23), .in23(OTMSB_24), .in24(OTMSB_25),
    .in25(OTMSB_26), .in26(OTMSB_27), .in27(OTMSB_28), .in28(OTMSB_29), .in29(OTMSB_30), .in30(OTMSB_31),
    .in31(OTMSB_32), .out(MSB_minus), .sel(VRS));
  Multiplexer #(.select(5), .width(16), .enable("false")) multiplexer_6 (
    .in0(OTLSB_1), .in1(OTLSB_2), .in2(OTLSB_3), .in3(OTLSB_4), .in4(OTLSB_5), .in5(OTLSB_6), .in6(OTLSB_7),
    .in7(OTLSB_8), .in8(OTLSB_9), .in9(OTLSB_10), .in10(OTLSB_11), .in11(OTLSB_12), .in12(OTLSB_13),
    .in13(OTLSB_14), .in14(OTLSB_15), .in15(OTLSB_16), .in16(OTLSB_17), .in17(OTLSB_18), .in18(OTLSB_19),
    .in19(OTLSB_20), .in20(OTLSB_21), .in21(OTLSB_22), .in22(OTLSB_23), .in23(OTLSB_24), .in24(OTLSB_25),
    .in25(OTLSB_26), .in26(OTLSB_27), .in27(OTLSB_28), .in28(OTLSB_29), .in29(OTLSB_30), .in30(OTLSB_31),
    .in31(OTLSB_32), .out(LSB_minus), .sel(VRS));
  Multiplexer #(.select(5), .width(16), .enable("false")) multiplexer_7 (
    .in0(OTMSB2_1), .in1(OTMSB2_2), .in2(OTMSB2_3), .in3(OTMSB2_4), .in4(OTMSB2_5), .in5(OTMSB2_6),
    .in6(OTMSB2_7), .in7(OTMSB2_8), .in8(OTMSB2_9), .in9(OTMSB2_10), .in10(OTMSB2_11), .in11(OTMSB2_12),
    .in12(OTMSB2_13), .in13(OTMSB2_14), .in14(OTMSB2_15), .in15(OTMSB2_16), .in16(OTMSB2_17),
    .in17(OTMSB2_18), .in18(OTMSB2_19), .in19(OTMSB2_20), .in20(OTMSB2_21), .in21(OTMSB2_22),
    .in22(OTMSB2_23), .in23(OTMSB2_24), .in24(OTMSB2_25), .in25(OTMSB2_26), .in26(OTMSB2_27),
    .in27(OTMSB2_28), .in28(OTMSB2_29), .in29(OTMSB2_30), .in30(OTMSB2_31), .in31(OTMSB2_32),
    .out(MSB2_minus), .sel(VRS));
  Multiplexer #(.select(5), .width(16), .enable("false")) multiplexer_8 (
    .in0(OTLSB2_1), .in1(OTLSB2_2), .in2(OTLSB2_3), .in3(OTLSB2_4), .in4(OTLSB2_5), .in5(OTLSB2_6),
    .in6(OTLSB2_7), .in7(OTLSB2_8), .in8(OTLSB2_9), .in9(OTLSB2_10), .in10(OTLSB2_11), .in11(OTLSB2_12),
    .in12(OTLSB2_13), .in13(OTLSB2_14), .in14(OTLSB2_15), .in15(OTLSB2_16), .in16(OTLSB2_17),
    .in17(OTLSB2_18), .in18(OTLSB2_19), .in19(OTLSB2_20), .in20(OTLSB2_21), .in21(OTLSB2_22),
    .in22(OTLSB2_23), .in23(OTLSB2_24), .in24(OTLSB2_25), .in25(OTLSB2_26), .in26(OTLSB2_27),
    .in27(OTLSB2_28), .in28(OTLSB2_29), .in29(OTLSB2_30), .in30(OTLSB2_31), .in31(OTLSB2_32),
    .out(LSB2_minus), .sel(VRS));

  // Other names for the same wires on the sheet: CLK = Clock; OT_1[4:0] = VRD; OT_2[4:0] = VRS; OTLSB[15:0] = LSB_2;
  //   OTLSB2[15:0] = LSB2_2; OTLSB2_minus[15:0] = LSB2_minus; OTLSB_minus[15:0] = LSB_minus; OTMSB[15:0] = MSB_2;
  //   OTMSB2[15:0] = MSB2_2; OTMSB2_minus[15:0] = MSB2_minus; OTMSB_minus[15:0] = MSB_minus; VRD_t[4:0] = origVRD;
  //   VRS_t[4:0] = origVRS

  // Notes on the sheet:
  //   64 Bit Input
  //   64 Bit Output 2
  //   64 Bit Output 1
  //   64 Bit Output 1 LSB
  //   64 Bit Output 1 MSB
  //   64 Bit Output 2 MSB
  //   64 Bit Output 2 LSB
endmodule

module ALU (
  input  [15:0] Input_1,
  input  [15:0] Input_1_2,
  input  [15:0] Input_1_3,
  input  [15:0] Input_1_4,
  input  [15:0] Input_2,
  input  [15:0] Input_2_2,
  input  [15:0] Input_2_3,
  input  [15:0] Input_2_4,
  input  [3:0] opcode,
  output [15:0] Output,
  output [15:0] Output_2,
  output [15:0] Output_3,
  output [15:0] Output_4
);

  wire comparator_1_eq, comparator_2_eq, comparator_3_eq, extend;
  wire [15:0] alu_sub_component_1_output, alu_sub_component_2_output, alu_sub_component_3_output,
       alu_sub_component_4_output, bit_extender_1_out, bit_extender_2_out, bit_extender_3_out,
       bit_extender_4_out, bit_extender_5_out, bit_extender_6_out, bit_extender_7_out, bit_extender_8_out,
       multiplexer_1_out, multiplexer_2_out, multiplexer_3_out, multiplexer_4_out;

  Comparator #(.width(3)) comparator_1 (.a(opcode[2:0]), .b(3'b001), .eq(comparator_1_eq));  // open: gt, lt
  Comparator #(.width(4)) comparator_2 (.a(opcode), .b(4'b1000), .eq(comparator_2_eq));  // open: gt, lt
  Comparator #(.width(4)) comparator_3 (.a(opcode), .b(4'b1001), .eq(comparator_3_eq));  // open: gt, lt
  assign bit_extender_1_out = {{8{Input_2[7]}}, Input_2[7:0]};  // Bit_Extender bit_extender_1
  assign bit_extender_2_out = {{8{1'b0}}, Input_2[7:0]};  // Bit_Extender bit_extender_2
  assign bit_extender_3_out = {{8{Input_2_2[7]}}, Input_2_2[7:0]};  // Bit_Extender bit_extender_3
  assign bit_extender_4_out = {{8{1'b0}}, Input_2_2[7:0]};  // Bit_Extender bit_extender_4
  assign bit_extender_5_out = {{8{Input_2_3[7]}}, Input_2_3[7:0]};  // Bit_Extender bit_extender_5
  assign bit_extender_6_out = {{8{1'b0}}, Input_2_3[7:0]};  // Bit_Extender bit_extender_6
  assign bit_extender_7_out = {{8{Input_2_4[7]}}, Input_2_4[7:0]};  // Bit_Extender bit_extender_7
  assign bit_extender_8_out = {{8{1'b0}}, Input_2_4[7:0]};  // Bit_Extender bit_extender_8
  or or_1 (extend, comparator_2_eq, comparator_3_eq);
  Multiplexer #(.width(16), .enable("false")) multiplexer_1 (
    .in0(bit_extender_1_out), .in1(bit_extender_2_out), .out(multiplexer_1_out), .sel(comparator_1_eq));
  Multiplexer #(.width(16), .enable("false")) multiplexer_2 (
    .in0(bit_extender_3_out), .in1(bit_extender_4_out), .out(multiplexer_2_out), .sel(comparator_1_eq));
  Multiplexer #(.width(16), .enable("false")) multiplexer_3 (
    .in0(bit_extender_5_out), .in1(bit_extender_6_out), .out(multiplexer_3_out), .sel(comparator_1_eq));
  Multiplexer #(.width(16), .enable("false")) multiplexer_4 (
    .in0(bit_extender_7_out), .in1(bit_extender_8_out), .out(multiplexer_4_out), .sel(comparator_1_eq));
  ALU_Sub_Component alu_sub_component_1 (
    .Input(Input_1), .Output(alu_sub_component_1_output), .Input2(Input_2), .opcode(opcode));
  ALU_Sub_Component alu_sub_component_2 (
    .Input(Input_1_2), .Output(alu_sub_component_2_output), .Input2(Input_2_2), .opcode(opcode));
  ALU_Sub_Component alu_sub_component_3 (
    .Input(Input_1_3), .Output(alu_sub_component_3_output), .Input2(Input_2_3), .opcode(opcode));
  ALU_Sub_Component alu_sub_component_4 (
    .Input(Input_1_4), .Output(alu_sub_component_4_output), .Input2(Input_2_4), .opcode(opcode));
  Multiplexer #(.width(16), .enable("false")) multiplexer_5 (
    .in0(alu_sub_component_1_output), .in1(multiplexer_1_out), .out(Output), .sel(extend));
  Multiplexer #(.width(16), .enable("false")) multiplexer_6 (
    .in0(alu_sub_component_2_output), .in1(multiplexer_2_out), .out(Output_2), .sel(extend));
  Multiplexer #(.width(16), .enable("false")) multiplexer_7 (
    .in0(alu_sub_component_3_output), .in1(multiplexer_3_out), .out(Output_3), .sel(extend));
  Multiplexer #(.width(16), .enable("false")) multiplexer_8 (
    .in0(alu_sub_component_4_output), .in1(multiplexer_4_out), .out(Output_4), .sel(extend));

  // Other names for the same wires on the sheet: _2_bit_op[3:0] = opcode; _4_bit_op[3:0] = opcode;
  //   Input1_1[15:0] = Input_1; Input1_2[15:0] = Input_1_2; Input1_3[15:0] = Input_1_3; Input1_4[15:0] = Input_1_4;
  //   Input2_1[15:0] = Input_2; Input2_2[15:0] = Input_2_2; Input2_3[15:0] = Input_2_3; Input2_4[15:0] = Input_2_4;
  //   Output1[15:0] = Output; Output2[15:0] = Output_2; Output3[15:0] = Output_3; Output4[15:0] = Output_4

  // Notes on the sheet:
  //   vb2ws - 101000
  //   vb2wz - 101001
  //   vw2bh - 100110
  //   vw2bl - 100111
  //   vadd - 101011
  //   vsub - 101100
  //   vmul - 101101
  //   vdiv - 101110
endmodule

module ALU_Sub_Component (
  input  [15:0] Input,
  input  [15:0] Input2,
  input  [3:0] opcode,
  output [15:0] Output
);

  wire [15:0] adder_1_out, bit_extender_1_out, bit_extender_2_out, divider_1_out, multiplier_1_out,
       subtractor_1_out;

  assign bit_extender_1_out = {{8{1'b0}}, Input[15:8]};  // Bit_Extender bit_extender_1
  assign bit_extender_2_out = {{8{1'b0}}, Input[7:0]};  // Bit_Extender bit_extender_2
  Adder #(.width(16)) adder_1 (.a(Input), .b(Input2), .out(adder_1_out));  // open: cin, cout
  Subtractor #(.width(16)) subtractor_1 (.a(Input), .b(Input2), .out(subtractor_1_out));  // open: bin, bout
  Multiplier #(.width(16)) multiplier_1 (.a(Input), .b(Input2), .out(multiplier_1_out));  // open: cin, cout
  Divider #(.width(16)) divider_1 (.a(Input), .b(Input2), .out(divider_1_out));  // open: upper, rem
  Multiplexer #(.select(4), .width(16), .enable("false")) multiplexer_1 (
    .in6(bit_extender_1_out), .in7(bit_extender_2_out), .in11(adder_1_out), .in12(subtractor_1_out),
    .in13(multiplier_1_out), .in14(divider_1_out), .out(Output), .sel(opcode));  // open: in0, in1, in2, in3, in4, in5, in8, in9, in10, in15

  // Notes on the sheet:
  //   vw2bh - 100110
  //   vw2bl - 100111
  //   vadd - 101011
  //   vsub - 101100
  //   vmul - 101101
  //   vdiv - 101110
endmodule

module Control (
  input  [5:0] vop,
  input  EX,
  output vcfg,
  output [3:0] _4_bit_opcode,
  output sv,
  output WriteEnable
);

  wire lv, lvi, lviu, lvr, not_1_out, not_2_out, not_3_out, not_4_out, not_5_out, or_1_out, vadd, vb2ws,
       vb2wz, vdiv, vmov, vmul, vsub, vw2bh, vw2bl;

  not not_1 (not_1_out, vop[2]);
  not not_2 (not_2_out, vop[3]);
  not not_3 (not_3_out, vop[4]);
  not not_4 (not_4_out, vop[0]);
  not not_5 (not_5_out, vop[1]);
  and u_vcfg (vcfg, not_4_out, not_5_out, not_1_out, not_2_out, not_3_out, vop[5]);
  and u_lv (lv, vop[0], not_5_out, not_1_out, not_2_out, not_3_out, vop[5]);
  and u_sv (sv, not_4_out, vop[1], not_1_out, not_2_out, not_3_out, vop[5]);
  and u_lvi (lvi, vop[0], vop[1], not_1_out, not_2_out, not_3_out, vop[5]);
  and u_lviu (lviu, not_4_out, not_5_out, vop[2], not_2_out, not_3_out, vop[5]);
  and u_lvr (lvr, vop[0], not_5_out, vop[2], not_2_out, not_3_out, vop[5]);
  and u_vw2bh (vw2bh, not_4_out, vop[1], vop[2], not_2_out, not_3_out, vop[5]);
  and u_vw2bl (vw2bl, vop[0], vop[1], vop[2], not_2_out, not_3_out, vop[5]);
  and u_vb2ws (vb2ws, not_4_out, not_5_out, not_1_out, vop[3], not_3_out, vop[5]);
  and u_vb2wz (vb2wz, vop[0], not_5_out, not_1_out, vop[3], not_3_out, vop[5]);
  and u_vmov (vmov, not_4_out, vop[1], not_1_out, vop[3], not_3_out, vop[5]);
  and u_vadd (vadd, vop[0], vop[1], not_1_out, vop[3], not_3_out, vop[5]);
  and u_vsub (vsub, not_4_out, not_5_out, vop[2], vop[3], not_3_out, vop[5]);
  and u_vmul (vmul, vop[0], not_5_out, vop[2], vop[3], not_3_out, vop[5]);
  and u_vdiv (vdiv, not_4_out, vop[1], vop[2], vop[3], not_3_out, vop[5]);
  or or_1 (or_1_out, lv, lvi, lviu, lvr, vw2bh, vw2bl, vb2ws, vb2wz, vmov, vadd, vsub, vmul, vdiv);
  and and_1 (WriteEnable, or_1_out, EX);

  assign _4_bit_opcode = vop[3:0];

  // Other names for the same wires on the sheet: opc[3:0] = vop[3:0]
endmodule
